// Logisim project 动态分支预测.circ as structural Verilog: 15 circuits, main circuit ◇单周期MIPS流水线
module \单周期MIPS流水线  (
);

  wire and_1_out, and_3_out, and_4_out, and_5_out, and_6_out, and_8_out, and_10_out, and_11_out, and_12_out,
       and_13_out, CLK, comparator_1_eq, comparator_2_eq, con_if, conBranch, \continue , ex_mem_1_out_17,
       ex_mem_1_out_18, ex_mem_1_out_20, ex_mem_1_out_21, ex_mem_1_out_22, ex_mem_1_out_29, EX_MemToReg,
       EX_RegWrite, Go, HALT, hasBranch, id_ex_1_out_29, id_ex_1_out_30, id_ex_1_out_33, id_ex_1_out_34,
       id_ex_1_out_36, id_ex_1_out_37, id_ex_1_out_39, id_ex_1_out_40, id_ex_1_out_41, id_ex_1_out_53,
       if_id_1_out_11, jal, JR, LoadUse, MEM_RegWrite, mem_wb_1_out_15, mips_alu_1_equal, or_2_out, or_3_out,
       or_4_out, or_7_out, or_8_out, or_9_out, or_10_out, R1_EX_Related, R1_MEM_Related, R1_Used,
       R2_EX_Related, R2_MEM_Related, R2_Used, RegWrite, RST, SignedExt, Success, Syscall, syscall_t,
       uncon_if, \硬布线控制器_1_alu_src , \硬布线控制器_1_beq , \硬布线控制器_1_bgez , \硬布线控制器_1_bne , \硬布线控制器_1_jmp ,
       \硬布线控制器_1_jr , \硬布线控制器_1_memaccess , \硬布线控制器_1_memtoreg , \硬布线控制器_1_memwrite , \硬布线控制器_1_regdst ,
       \硬布线控制器_1_regwrite ;
  wire [0:0] or_1_out, or_6_out;
  wire [1:0] id_ex_1_out_42, id_ex_1_out_43;
  wire [3:0] id_ex_1_out_38, multiplexer_12_out, multiplexer_13_out, \硬布线控制器_1_alu_op ;
  wire [4:0] EX_WriteReg_num, id_ex_1_out_48, MEM_WriteReg_num, multiplexer_6_out, R1_num, R2_num, Rd, rd_t;
  wire [5:0] if_id_1_out_10_3;
  wire [15:0] if_id_1_out_10, \LoadUse数 , multiplexer_14_out, \总周期数 , \插入气泡数 , \无条件分支数 , \条件分支成功数 , \预测成功数 ;
  wire [25:0] id_ex_1_out_49;
  wire [25:16] if_id_1_out_10_2;
  wire [31:0] b_pc, bit_extender_1_out, bit_extender_2_out, bit_extender_3_out, branch_pc, branchPC, EX_IR,
       ex_mem_1_out_23, ex_mem_1_out_24, ex_mem_1_out_25, ex_mem_1_out_27, ex_mem_1_out_28, EX_PC,
       EX_PredictPC, EX_Redirect, id_ex_1_out_44, id_ex_1_out_45, id_ex_1_out_47, if_id_1_out_8,
       if_id_1_out_9, IF_PC, j_pc, jr_pc, LedData, MEM_Redirect, mem_wb_1_out_21, mem_wb_1_out_22,
       mips_alu_1_result, mips_ram_1_p5, mips_regifile_1_r1, mips_regifile_1_r2, multiplexer_2_out,
       multiplexer_8_out, multiplexer_9_out, multiplexer_11_out, multiplexer_15_out, multiplexer_17_out,
       next_pc, noneBranch, predict_pc, R1, R2, result2, rom_1_data, shifter_1_out;

  Button \u_总复位  (.out(RST));
  Button u_Go (.out(Go));
  Clock clock_1 (.out(CLK));
  or or_1 (or_1_out[0], JR, con_if);
  // Probe on branch_pc
  // Probe on predict_pc
  Hex_Digit_Display hex_digit_display_1 (.value(LedData[31:28]));  // open: dp
  Hex_Digit_Display hex_digit_display_2 (.value(LedData[27:24]));  // open: dp
  // Probe on branch_pc
  Multiplexer #(.select(2), .width(32), .disabled(0), .enable("false")) multiplexer_1 (
    .in0(noneBranch), .in1(b_pc), .in2(j_pc), .in3(jr_pc), .out(branch_pc), .sel({uncon_if, or_1_out[0]}));
  // Probe on multiplexer_2_out
  Multiplexer #(.width(32), .disabled(0), .enable("false")) multiplexer_2 (
    .in0(branch_pc), .in1(predict_pc), .out(multiplexer_2_out), .sel(\continue ));
  or or_2 (or_2_out, Go, ~HALT);  // OR_Gate
  Hex_Digit_Display hex_digit_display_3 (.value(LedData[19:16]));  // open: dp
  Hex_Digit_Display hex_digit_display_4 (.value(LedData[23:20]));  // open: dp
  Comparator #(.width(32)) comparator_1 (.a(branch_pc), .b(EX_PredictPC), .eq(comparator_1_eq));  // open: gt, lt
  and and_1 (and_1_out, or_2_out, ~LoadUse);  // AND_Gate
  BHT bht_1 (
    .IF_PC(IF_PC), .EX_PC(EX_PC), .BranchPC(branch_pc), .Success(Success), .PredictAddr(predict_pc),
    .clk(CLK), .hasBranch(hasBranch));
  Hex_Digit_Display hex_digit_display_5 (.value(LedData[11:8]));  // open: dp
  Hex_Digit_Display hex_digit_display_6 (.value(LedData[15:12]));  // open: dp
  and and_2 (Success, comparator_1_eq, hasBranch);
  Register #(.width(32)) PC (.D(multiplexer_2_out), .en(and_1_out), .Q(IF_PC), .clk(CLK), .clr(RST));
  Hex_Digit_Display hex_digit_display_7 (.value(LedData[3:0]));  // open: dp
  Hex_Digit_Display hex_digit_display_8 (.value(LedData[7:4]));  // open: dp
  \数据相关检测  \u_数据相关检测_1  (
    .R1_EX_Related(R1_EX_Related), .R1_MEM_Related(R1_MEM_Related), .R1_Used(R1_Used), .R2_Used(R2_Used),
    .EX_RegWrite(EX_RegWrite), .MEM_RegWrite(MEM_RegWrite), .R1_num(R1_num), .R2_num(R2_num),
    .EX_WriteReg_num(EX_WriteReg_num), .MEM_WriteReg_num(MEM_WriteReg_num), .R2_EX_Related(R2_EX_Related),
    .R2_MEM_Related(R2_MEM_Related));
  or or_3 (or_3_out, ~\continue , LoadUse);  // OR_Gate
  // Probe on IF_PC
  Counter #(.width(16), .max('hffff)) counter_1 (
    .count(and_3_out), .Q(\LoadUse数 ), .clk(CLK), .clr(RST));  // open: load, D, carry
  and and_3 (and_3_out, LoadUse, ~HALT);  // AND_Gate
  Counter #(.width(16), .max('hffff)) counter_2 (
    .count(and_4_out), .Q(\预测成功数 ), .clk(CLK), .clr(RST));  // open: load, D, carry
  and and_4 (and_4_out, Success, ~HALT);  // AND_Gate
  Counter #(.width(16), .max('hffff)) counter_3 (
    .count(and_5_out), .Q(\插入气泡数 ), .clk(CLK), .clr(RST));  // open: load, D, carry
  and and_5 (and_5_out, or_3_out, ~HALT);  // AND_Gate
  Counter #(.width(16), .max('hffff)) counter_4 (
    .count(con_if), .Q(\条件分支成功数 ), .clk(CLK), .clr(RST));  // open: load, D, carry
  Counter #(.width(16), .max('hffff)) counter_5 (
    .count(uncon_if), .Q(\无条件分支数 ), .clk(CLK), .clr(RST));  // open: load, D, carry
  Counter #(.width(16), .max('hffff)) counter_6 (
    .count(or_4_out), .Q(\总周期数 ), .clk(CLK), .clr(RST));  // open: load, D, carry
  or or_4 (or_4_out, Go, ~HALT);  // OR_Gate
  or or_5 (\continue , ~hasBranch, Success);  // OR_Gate
  Adder #(.width(32)) adder_1 (.a(IF_PC), .b(32'h4), .out(next_pc));  // open: cin, cout
  ROM #(.addrWidth(10), .dataWidth(32)) rom_1 (.addr(IF_PC[11:2]), .data(rom_1_data));  // open: sel
  // Probe on next_pc
  // Probe on \总周期数 
  // Probe on \无条件分支数 
  // Probe on \条件分支成功数 
  // Probe on \插入气泡数 
  and and_6 (and_6_out, ~Go, HALT);  // AND_Gate
  or or_6 (or_6_out[0], JR, conBranch);
  or or_7 (or_7_out, RST, ~\continue );  // OR_Gate
  or or_8 (or_8_out, LoadUse, and_6_out);
  Multiplexer #(.select(2), .width(32), .disabled(0), .enable("false")) multiplexer_3 (
    .in0(noneBranch), .in1(b_pc), .in2(j_pc), .in3(jr_pc), .out(branchPC), .sel({uncon_if, or_6_out[0]}));
  // Probe on \LoadUse数 
  // Probe on \预测成功数 
  IF_ID if_id_1 (
    .IR(rom_1_data), .Clear(or_7_out), .out_10({if_id_1_out_10_3, if_id_1_out_10_2, if_id_1_out_10}),
    .Enable(or_8_out), .clk(CLK), .PC(next_pc), .out_8(if_id_1_out_8), .Effective(1'b1),
    .out_11(if_id_1_out_11), .PredictPC(predict_pc), .out_9(if_id_1_out_9));
  // Probe on if_id_1_out_8
  or or_9 (or_9_out, R1_EX_Related, R2_EX_Related);
  // Probe on R1
  and and_7 (LoadUse, EX_MemToReg, or_9_out);
  \源寄存器使用情况  \u_源寄存器使用情况_1  (.R1_Used(R1_Used), .R2_Used(R2_Used), .OP(if_id_1_out_10_3), .Func(if_id_1_out_10[5:0]));
  Comparator #(.width(32)) comparator_2 (.a(R1), .b(32'h22), .eq(comparator_2_eq));  // open: gt, lt
  \硬布线控制器  \u_硬布线控制器_1  (
    .Func(if_id_1_out_10[5:0]), .OP(if_id_1_out_10_3), .ALU_OP(\硬布线控制器_1_alu_op ),
    .MemToReg(\硬布线控制器_1_memtoreg ), .MemWrite(\硬布线控制器_1_memwrite ), .ALU_SRC(\硬布线控制器_1_alu_src ),
    .RegWrite(\硬布线控制器_1_regwrite ), .SysCall(syscall_t), .SignedExt(SignedExt), .RegDst(\硬布线控制器_1_regdst ),
    .JR(\硬布线控制器_1_jr ), .JMP(\硬布线控制器_1_jmp ), .Beq(\硬布线控制器_1_beq ), .JAL(jal), .Bne(\硬布线控制器_1_bne ),
    .MemAccess(\硬布线控制器_1_memaccess ), .BGEZ(\硬布线控制器_1_bgez ));
  Multiplexer #(.width(5), .enable("false")) multiplexer_4 (
    .in0(if_id_1_out_10_2[25:21]), .in1(5'b00010), .out(R1_num), .sel(syscall_t));
  Multiplexer #(.width(5), .enable("false")) multiplexer_5 (
    .in0(if_id_1_out_10_2[20:16]), .in1(5'b00100), .out(R2_num), .sel(syscall_t));
  Multiplexer #(.width(5), .enable("false")) multiplexer_6 (
    .in0(if_id_1_out_10_2[20:16]), .in1(if_id_1_out_10[15:11]), .out(multiplexer_6_out),
    .sel(\硬布线控制器_1_regdst ));
  assign bit_extender_1_out = {{16{1'b0}}, if_id_1_out_10};  // Bit_Extender bit_extender_1
  assign bit_extender_2_out = {{16{if_id_1_out_10[15]}}, if_id_1_out_10};  // Bit_Extender bit_extender_2
  and and_8 (and_8_out, Syscall, comparator_2_eq);
  and and_9 (HALT, ~comparator_2_eq, Syscall);  // AND_Gate
  Multiplexer #(.width(5), .enable("false")) multiplexer_7 (
    .in0(multiplexer_6_out), .in1({5{1'b1}}), .out(rd_t), .sel(jal));
  Register #(.width(32)) Led (.D(R2), .en(and_8_out), .Q(LedData), .clk(CLK), .clr(RST));
  Multiplexer #(.width(32), .enable("false")) multiplexer_8 (
    .in0(bit_extender_1_out), .in1(bit_extender_2_out), .out(multiplexer_8_out), .sel(SignedExt));
  or or_10 (or_10_out, RST, ~\continue , LoadUse);  // OR_Gate
  MIPS_Regifile mips_regifile_1 (
    .Din(multiplexer_17_out), .Clk(CLK), .R1(mips_regifile_1_r1), .R2(mips_regifile_1_r2), .WE(RegWrite),
    .W_num(Rd), .R1_num(R1_num), .R2_num(R2_num));
  and and_10 (and_10_out, ~Go, HALT);  // AND_Gate
  ID_EX id_ex_1 (
    .IR({if_id_1_out_10_3, if_id_1_out_10_2, if_id_1_out_10}), .out_52(EX_IR), .PC(if_id_1_out_8),
    .out_50(noneBranch), .Clear(or_10_out), .clk(CLK), .Effective(if_id_1_out_11), .out_53(id_ex_1_out_53),
    .R2(mips_regifile_1_r2), .out_45(id_ex_1_out_45), .R1(mips_regifile_1_r1), .out_44(id_ex_1_out_44),
    .Imm(multiplexer_8_out), .out_47(id_ex_1_out_47), .Shamt(if_id_1_out_10[10:6]), .out_48(id_ex_1_out_48),
    .j_addr({if_id_1_out_10_2, if_id_1_out_10}), .out_49(id_ex_1_out_49), .Enable(and_10_out),
    .out_29(id_ex_1_out_29), .out_30(id_ex_1_out_30), .out_32(EX_MemToReg), .out_33(id_ex_1_out_33),
    .out_34(id_ex_1_out_34), .out_35(JR), .out_36(id_ex_1_out_36), .out_37(id_ex_1_out_37),
    .out_39(id_ex_1_out_39), .out_38(id_ex_1_out_38), .R1_Forward({R1_EX_Related, R1_MEM_Related}),
    .out_42(id_ex_1_out_42), .Syscall(syscall_t), .JAL(jal), .MemToReg(\硬布线控制器_1_memtoreg ),
    .MemWrite(\硬布线控制器_1_memwrite ), .JR(\硬布线控制器_1_jmp ), .JMP(\硬布线控制器_1_jr ), .Beq(\硬布线控制器_1_beq ),
    .Bne(\硬布线控制器_1_bne ), .AluOP(\硬布线控制器_1_alu_op ), .AluSrcB(\硬布线控制器_1_alu_src ),
    .RegWrite(\硬布线控制器_1_regwrite ), .out_31(EX_RegWrite), .R2_Forward({R2_EX_Related, R2_MEM_Related}),
    .out_43(id_ex_1_out_43), .Rd(rd_t), .out_46(EX_WriteReg_num), .MemAccess(\硬布线控制器_1_memaccess ),
    .out_40(id_ex_1_out_40), .BGEZ(\硬布线控制器_1_bgez ), .out_41(id_ex_1_out_41), .PredictPC(if_id_1_out_9),
    .out_51(EX_PredictPC));
  // Probe on noneBranch
  Multiplexer #(.select(2), .width(32), .enable("false")) multiplexer_9 (
    .in0(id_ex_1_out_45), .in1(MEM_Redirect), .in2(EX_Redirect), .in3(EX_Redirect), .out(multiplexer_9_out),
    .sel(id_ex_1_out_43));
  Shifter #(.width(32)) shifter_1 (.in(id_ex_1_out_47), .\dist (5'b00010), .out(shifter_1_out));
  assign bit_extender_3_out = {{6{1'b0}}, id_ex_1_out_49};  // Bit_Extender bit_extender_3
  Multiplexer #(.select(2), .width(32), .enable("false")) multiplexer_10 (
    .in0(id_ex_1_out_44), .in1(MEM_Redirect), .in2(EX_Redirect), .in3(EX_Redirect), .out(jr_pc),
    .sel(id_ex_1_out_42));
  Multiplexer #(.width(32), .enable("false")) multiplexer_11 (
    .in0(multiplexer_9_out), .in1(id_ex_1_out_47), .out(multiplexer_11_out), .sel(id_ex_1_out_39));
  Adder #(.width(32)) adder_2 (.a(shifter_1_out), .b(noneBranch), .out(b_pc));  // open: cin, cout
  Shifter #(.width(32)) shifter_2 (.in(bit_extender_3_out), .\dist (5'b00010), .out(j_pc));
  MIPS_ALU mips_alu_1 (
    .X(jr_pc), .Y(multiplexer_11_out), .AluOP(id_ex_1_out_38), .Equal(mips_alu_1_equal),
    .Result(mips_alu_1_result), .Result_2(result2), .shamt(id_ex_1_out_48));
  or or_11 (conBranch, id_ex_1_out_41, id_ex_1_out_37, id_ex_1_out_36);
  or or_12 (uncon_if, id_ex_1_out_30, id_ex_1_out_34, JR);
  and and_11 (and_11_out, mips_alu_1_equal, id_ex_1_out_36);
  and and_12 (and_12_out, id_ex_1_out_37, ~mips_alu_1_equal);  // AND_Gate
  or or_13 (con_if, and_11_out, and_12_out, and_13_out);
  and and_13 (and_13_out, id_ex_1_out_41, ~mips_alu_1_result[0]);  // AND_Gate
  or or_14 (hasBranch, id_ex_1_out_30, id_ex_1_out_34, JR, id_ex_1_out_36, id_ex_1_out_37, id_ex_1_out_41);
  Subtractor #(.width(32)) subtractor_1 (.a(noneBranch), .b(32'h4), .out(EX_PC));  // open: bin, bout
  EX_MEM ex_mem_1 (
    .alu_result1(mips_alu_1_result), .out_23(ex_mem_1_out_23), .IR(noneBranch), .out_27(ex_mem_1_out_27),
    .PC(EX_IR), .out_28(ex_mem_1_out_28), .Effective(id_ex_1_out_53), .out_29(ex_mem_1_out_29), .Clear(RST),
    .Enable(and_10_out), .clk(CLK), .out_20(ex_mem_1_out_20), .out_21(ex_mem_1_out_21),
    .MemToReg(EX_MemToReg), .MemWrite(id_ex_1_out_33), .JAL(id_ex_1_out_30), .out_18(ex_mem_1_out_18),
    .Syscall(id_ex_1_out_29), .out_17(ex_mem_1_out_17), .R1(jr_pc), .out_24(ex_mem_1_out_24),
    .R2(multiplexer_9_out), .out_25(ex_mem_1_out_25), .Rd(EX_WriteReg_num), .out_26(MEM_WriteReg_num),
    .RegWrite(EX_RegWrite), .out_19(MEM_RegWrite), .MemAccess(id_ex_1_out_40), .out_22(ex_mem_1_out_22));
  Multiplexer #(.width(4), .enable("false")) multiplexer_12 (
    .in0(4'b1111), .in1(multiplexer_13_out), .out(multiplexer_12_out), .sel(ex_mem_1_out_22));
  Multiplexer #(.width(4), .enable("false")) multiplexer_13 (
    .in0(4'b0011), .in1(4'b1100), .out(multiplexer_13_out), .sel(ex_mem_1_out_23[1]));
  // Probe on ex_mem_1_out_27
  // MIPS_RAM mips_ram_1: pin names not known; wires that end beside it: ex_mem_1_out_23[11:2], ex_mem_1_out_21, multiplexer_12_out, CLK, mips_ram_1_p5
  Multiplexer #(.width(16), .enable("false")) multiplexer_14 (
    .in0(mips_ram_1_p5[15:0]), .in1(mips_ram_1_p5[31:16]), .out(multiplexer_14_out), .sel(ex_mem_1_out_23[1]));
  Multiplexer #(.width(32), .enable("false")) multiplexer_15 (
    .in0(mips_ram_1_p5), .in1({{16{1'b1}}, multiplexer_14_out}), .out(multiplexer_15_out),
    .sel(ex_mem_1_out_22));
  Multiplexer #(.width(32), .enable("false")) multiplexer_16 (
    .in0(ex_mem_1_out_23), .in1(multiplexer_15_out), .out(EX_Redirect), .sel(ex_mem_1_out_20));
  MEM_WB mem_wb_1 (
    .write_back(EX_Redirect), .out_20(MEM_Redirect), .IR(ex_mem_1_out_27), .out_21(mem_wb_1_out_21),
    .PC(ex_mem_1_out_28), .out_22(mem_wb_1_out_22), .Effective(ex_mem_1_out_29), .Clear(RST),
    .Enable(and_10_out), .clk(CLK), .R1(ex_mem_1_out_24), .out_17(R1), .Syscall(ex_mem_1_out_17),
    .out_14(Syscall), .JAL(ex_mem_1_out_18), .out_15(mem_wb_1_out_15), .R2(ex_mem_1_out_25), .out_18(R2),
    .Rd(MEM_WriteReg_num), .out_19(Rd), .RegWrite(MEM_RegWrite), .out_16(RegWrite));  // open: out_23
  Multiplexer #(.width(32), .enable("false")) multiplexer_17 (
    .in0(MEM_Redirect), .in1(mem_wb_1_out_21), .out(multiplexer_17_out), .sel(mem_wb_1_out_15));
  // Probe on MEM_Redirect
  // Probe on mem_wb_1_out_22

  // Notes on the sheet:
  //   数码管输出应该用寄存器锁存，否则显示数据只能一闪而过
  //   可以通过项目增加Logisim库的方式将前几次实验完成的电路作为子电路引入到本电路中使用
  //   数码管输出
  //   指令存储器
  //   指令字
  //   contents of rom_1 (hex, n*v repeats v):
  //   20110001 8000c05 20110001 20120002 20130003 8000c09 20110001 20120002 20130003 8000c0d 20110001
  //   20120002 20130003 8000c11 20110001 20120002 20130003 c000cf6 20100001 20110001 118fc0 112020
  //   20020022 c 118882 12200001 8000c15 112020 20020022 c 20110001 118880 112020 20020022 c 12200001
  //   8000c1f 20110001 118fc0 112020 20020022 c 1188c3 112020 20020022 c 118903 112020 20020022 c 118903
  //   112020 20020022 c 118903 112020 20020022 c 118903 112020 20020022 c 118903 112020 20020022 c 118903
  //   112020 20020022 c 118903 112020 20020022 c 20100001 109fc0 139fc3 8021 2012000c 24160003 26100001
  //   3210000f 20080008 20090001 139900 2709825 132020 20020022 c 1094022 1500fff9 22100001 2018000f
  //   2188024 108700 20080008 20090001 139902 2709825 132021 20020022 c 1094022 1500fff9 108702 2c9b022
  //   12c00001 8000c50 4020 1084027 84400 3508ffff 82021 20020022 c 2010ffff 20110000 ae300000 22100001
  //   22310004 ae300000 22100001 22310004 ae300000 22100001 22310004 ae300000 22100001 22310004 ae300000
  //   22100001 22310004 ae300000 22100001 22310004 ae300000 22100001 22310004 ae300000 22100001 22310004
  //   ae300000 22100001 22310004 ae300000 22100001 22310004 ae300000 22100001 22310004 ae300000 22100001
  //   22310004 ae300000 22100001 22310004 ae300000 22100001 22310004 ae300000 22100001 22310004 ae300000
  //   22100001 22310004 22100001 8020 2011003c 8e130000 8e340000 274402a 11000002 ae330000 ae140000
  //   2231fffc 1611fff8 102020 20020022 c 22100004 2011003c 1611fff2 20020032 c 20080001 20110010 112020
  //   20020022 c 200b0020 2288823 112020 20020022 c 216bffff 1560fffa 2002000a c 2008ffff 20117777 112020
  //   20020022 c 200b0010 3a31ffff 112020 20020022 c 216bffff 1560fffa 2002000a c 20090000 200b0010
  //   34118483 20120404 118c00 129400 36318281 22520404 ad310000 2328820 21290004 216bffff 1560fffb
  //   200b0020 20090000 85310000 112020 20020022 c 21290002 216bffff 1560fff9 2002000a c 2002000a c
  //   2011000f 112020 20020022 c 2231ffff 621fffb 2002000a c 20100000 22100001 102020 20020022 c 22100002
  //   102020 20020022 c 22100003 102020 20020022 c 22100004 102020 20020022 c 22100005 102020 20020022 c
  //   22100006 102020 20020022 c 22100007 102020 20020022 c 22100008 102020 20020022 20020022 c 3e00008
  //   总复位信号应将除ROM以外所有存储组件全部清零
  //   OP
  //   Func
  //   rs
  //   rt
  //   rd
  //   Imm
  //   shamt
  //   j-addr
  //   JMP
  //   JR
  //   Beq
  //   Bne
  //   BGEZ
  //   OP
  //   JAL
  //   Func
  //   RegWrite
  //   MemToReg
  //   MemWrite
  //   MemAccess
  //   AluOP
  //   AluSrcB
  //   RegDst
  //   Syscall
endmodule

// 单周期硬布线控制器
module \硬布线控制器  (
  input  [5:0] OP,
  input  [5:0] Func,
  output [3:0] ALU_OP,
  output MemAccess,
  output MemWrite,
  output JAL,
  output JMP,
  output ALU_SRC,
  output RegWrite,
  output SysCall,
  output MemToReg,
  output SignedExt,
  output RegDst,
  output Beq,
  output Bne,
  output JR,
  output BGEZ
);

  Comparator #(.width(6)) comparator_1 (.a(OP), .b(6'b100001), .eq(MemAccess));  // open: gt, lt
  \运算控制器  \u_运算控制器_1  (
    .OP0(OP[0]), .OP1(OP[1]), .OP2(OP[2]), .OP3(OP[3]), .OP4(OP[4]), .OP5(OP[5]), .F0(Func[0]), .F1(Func[1]),
    .F2(Func[2]), .F3(Func[3]), .F4(Func[4]), .F5(Func[5]), .S0(ALU_OP[0]), .S1(ALU_OP[1]), .S2(ALU_OP[2]),
    .S3(ALU_OP[3]));
  \控制信号生成  \u_控制信号生成_1  (
    .OP0(OP[0]), .MemWrite(MemWrite), .OP1(OP[1]), .OP2(OP[2]), .OP3(OP[3]), .JAL(JAL), .OP4(OP[4]),
    .OP5(OP[5]), .JMP(JMP), .F0(Func[0]), .F1(Func[1]), .F2(Func[2]), .F3(Func[3]), .F4(Func[4]),
    .F5(Func[5]), .ALU_SRC(ALU_SRC), .RegWrite(RegWrite), .SysCALL(SysCall), .MemtoReg(MemToReg),
    .SignedExt(SignedExt), .RegDst(RegDst), .BEQ(Beq), .BNE(Bne), .JR(JR), .BGEZ(BGEZ));

  // Other names for the same wires on the sheet: OP_CODE[5:0] = OP

  // Notes on the sheet:
  //   运算器控制器，根据指令生成运算器功能选择信号
  //   控制信号生成，产生数据通路需要的其他控制信号
endmodule

// 运算器控制器
module \运算控制器  (
  input  OP0,
  input  OP1,
  input  OP2,
  input  OP3,
  input  OP4,
  input  OP5,
  input  F0,
  input  F1,
  input  F2,
  input  F3,
  input  F4,
  input  F5,
  output S0,
  output S1,
  output S2,
  output S3
);

  wire and_1_out, and_2_out, and_3_out, and_4_out, and_5_out, and_6_out, and_7_out, and_8_out, and_9_out,
       and_10_out, and_11_out, and_12_out, and_13_out, and_14_out, and_15_out, and_16_out, and_17_out,
       and_18_out, and_19_out, and_20_out, and_21_out, and_22_out, and_23_out, and_24_out, and_25_out,
       and_26_out, and_27_out, and_28_out, and_29_out, and_30_out, and_31_out, and_32_out, and_33_out,
       and_34_out, and_35_out, and_36_out, and_37_out, and_38_out, and_39_out, and_40_out, and_41_out,
       and_42_out, and_43_out, and_44_out, and_45_out, and_46_out, and_47_out, and_48_out, and_49_out,
       not_1_out, not_2_out, not_3_out, not_4_out, not_5_out, not_6_out, not_7_out, not_8_out, not_9_out,
       not_10_out, not_11_out, not_12_out, not_13_out, not_14_out, not_15_out, not_16_out, not_17_out,
       not_18_out, not_19_out, not_20_out, not_21_out, not_22_out, not_23_out, not_24_out, not_25_out,
       not_26_out, not_27_out, not_28_out, not_29_out, not_30_out, not_31_out, not_32_out, not_33_out,
       not_34_out, not_35_out, not_36_out, not_37_out, not_38_out, not_39_out, not_40_out, not_41_out,
       not_42_out, not_43_out, not_44_out, not_45_out, not_46_out, not_47_out, not_48_out, not_49_out,
       not_50_out, not_51_out, not_52_out, not_53_out, not_54_out, not_55_out, not_56_out, not_57_out,
       not_58_out, not_59_out, not_60_out, not_61_out, not_62_out, not_63_out, not_64_out, not_65_out,
       not_66_out, not_67_out, not_68_out, not_69_out, not_70_out, not_71_out, not_72_out, not_73_out,
       not_74_out, not_75_out, not_76_out, not_77_out, not_78_out, not_79_out, not_80_out, not_81_out,
       not_82_out, not_83_out, not_84_out, not_85_out, not_86_out, not_87_out, not_88_out, not_89_out,
       not_90_out, not_91_out, not_92_out, not_93_out, not_94_out, not_95_out, not_96_out, not_97_out,
       not_98_out, not_99_out, not_100_out, not_101_out, not_102_out, not_103_out, not_104_out, not_105_out,
       not_106_out, not_107_out, not_108_out, not_109_out, not_110_out, not_111_out, not_112_out,
       not_113_out, not_114_out, not_115_out, not_116_out, not_117_out, not_118_out, not_119_out,
       not_120_out, not_121_out, not_122_out, not_123_out, not_124_out, not_125_out, not_126_out,
       not_127_out, not_128_out, not_129_out, not_130_out, not_131_out, not_132_out, not_133_out,
       not_134_out, not_135_out, not_136_out, not_137_out, not_138_out, not_139_out, not_140_out,
       not_141_out, not_142_out, not_143_out, not_144_out, not_145_out, not_146_out, not_147_out,
       not_148_out, not_149_out, not_150_out, not_151_out, not_152_out, not_153_out, not_154_out,
       not_155_out, not_156_out, not_157_out, not_158_out, not_159_out, not_160_out, not_161_out,
       not_162_out, not_163_out, not_164_out, not_165_out, not_166_out, not_167_out, not_168_out,
       not_169_out, not_170_out, not_171_out, not_172_out, not_173_out, not_174_out, not_175_out,
       not_176_out, not_177_out, not_178_out, not_179_out, not_180_out, not_181_out, not_182_out,
       not_183_out, not_184_out, not_185_out, not_186_out, not_187_out, not_188_out, not_189_out,
       not_190_out, not_191_out, not_192_out, not_193_out, not_194_out, not_195_out, not_196_out,
       not_197_out, not_198_out, not_199_out, not_200_out, not_201_out, not_202_out, not_203_out,
       not_204_out, not_205_out, not_206_out, not_207_out, not_208_out, not_209_out, not_210_out,
       not_211_out, not_212_out, not_213_out, not_214_out, not_215_out, not_216_out, not_217_out,
       not_218_out, not_219_out, not_220_out, not_221_out, not_222_out, not_223_out, not_224_out,
       not_225_out, not_226_out, not_227_out, not_228_out, not_229_out, not_230_out, not_231_out,
       not_232_out, not_233_out, not_234_out, not_235_out, not_236_out, not_237_out, not_238_out,
       not_239_out, not_240_out, not_241_out, not_242_out, not_243_out, not_244_out, not_245_out,
       not_246_out, not_247_out, not_248_out, not_249_out, not_250_out, not_251_out, not_252_out,
       not_253_out, not_254_out, not_255_out, not_256_out, not_257_out, not_258_out, not_259_out,
       not_260_out, not_261_out, not_262_out, not_263_out, not_264_out, not_265_out, not_266_out,
       not_267_out, not_268_out, not_269_out, not_270_out, not_271_out, not_272_out, not_273_out,
       not_274_out, not_275_out, not_276_out, not_277_out, not_278_out, not_279_out, not_280_out,
       not_281_out, not_282_out, not_283_out, not_284_out, not_285_out, not_286_out, not_287_out,
       not_288_out, not_289_out, not_290_out, not_291_out, not_292_out, not_293_out, not_294_out,
       not_295_out, not_296_out, not_297_out, not_298_out, not_299_out, not_300_out, not_301_out,
       not_302_out, not_303_out, not_304_out, not_305_out, not_306_out, not_307_out, not_308_out,
       not_309_out, not_310_out;

  not not_1 (not_1_out, OP5);
  not not_2 (not_2_out, OP4);
  not not_3 (not_3_out, OP3);
  not not_4 (not_4_out, OP2);
  not not_5 (not_5_out, OP1);
  not not_6 (not_6_out, OP0);
  not not_7 (not_7_out, F5);
  not not_8 (not_8_out, F4);
  not not_9 (not_9_out, F3);
  not not_10 (not_10_out, F2);
  not not_11 (not_11_out, OP5);
  not not_12 (not_12_out, OP4);
  not not_13 (not_13_out, OP3);
  not not_14 (not_14_out, OP2);
  not not_15 (not_15_out, OP1);
  not not_16 (not_16_out, OP0);
  not not_17 (not_17_out, F4);
  not not_18 (not_18_out, F3);
  not not_19 (not_19_out, F2);
  not not_20 (not_20_out, F1);
  not not_21 (not_21_out, F0);
  not not_22 (not_22_out, OP5);
  not not_23 (not_23_out, OP4);
  not not_24 (not_24_out, OP3);
  not not_25 (not_25_out, OP2);
  not not_26 (not_26_out, OP1);
  not not_27 (not_27_out, OP0);
  not not_28 (not_28_out, F4);
  not not_29 (not_29_out, F3);
  not not_30 (not_30_out, F2);
  not not_31 (not_31_out, F1);
  not not_32 (not_32_out, OP5);
  not not_33 (not_33_out, OP4);
  not not_34 (not_34_out, OP3);
  not not_35 (not_35_out, OP2);
  not not_36 (not_36_out, OP1);
  not not_37 (not_37_out, OP0);
  not not_38 (not_38_out, F4);
  not not_39 (not_39_out, F3);
  not not_40 (not_40_out, F1);
  not not_41 (not_41_out, F0);
  not not_42 (not_42_out, OP5);
  not not_43 (not_43_out, OP4);
  not not_44 (not_44_out, OP3);
  not not_45 (not_45_out, OP2);
  not not_46 (not_46_out, OP1);
  not not_47 (not_47_out, OP0);
  not not_48 (not_48_out, F4);
  not not_49 (not_49_out, F2);
  not not_50 (not_50_out, F0);
  not not_51 (not_51_out, OP5);
  not not_52 (not_52_out, OP4);
  not not_53 (not_53_out, OP3);
  not not_54 (not_54_out, OP1);
  not not_55 (not_55_out, OP0);
  not not_56 (not_56_out, OP5);
  not not_57 (not_57_out, OP4);
  not not_58 (not_58_out, OP3);
  not not_59 (not_59_out, OP1);
  not not_60 (not_60_out, OP5);
  not not_61 (not_61_out, OP4);
  not not_62 (not_62_out, OP2);
  not not_63 (not_63_out, OP1);
  not not_64 (not_64_out, OP0);
  not not_65 (not_65_out, OP5);
  not not_66 (not_66_out, OP4);
  not not_67 (not_67_out, OP1);
  not not_68 (not_68_out, OP0);
  not not_69 (not_69_out, OP5);
  not not_70 (not_70_out, OP4);
  not not_71 (not_71_out, OP2);
  not not_72 (not_72_out, OP1);
  not not_73 (not_73_out, OP5);
  not not_74 (not_74_out, OP4);
  not not_75 (not_75_out, OP2);
  not not_76 (not_76_out, OP0);
  not not_77 (not_77_out, OP4);
  not not_78 (not_78_out, OP3);
  not not_79 (not_79_out, OP2);
  not not_80 (not_80_out, OP4);
  not not_81 (not_81_out, OP2);
  not not_82 (not_82_out, OP5);
  not not_83 (not_83_out, OP4);
  not not_84 (not_84_out, OP0);
  not not_85 (not_85_out, OP4);
  not not_86 (not_86_out, OP3);
  not not_87 (not_87_out, OP2);
  not not_88 (not_88_out, OP1);
  not not_89 (not_89_out, OP5);
  not not_90 (not_90_out, OP4);
  not not_91 (not_91_out, OP3);
  not not_92 (not_92_out, OP2);
  not not_93 (not_93_out, OP1);
  not not_94 (not_94_out, OP5);
  not not_95 (not_95_out, OP4);
  not not_96 (not_96_out, OP3);
  not not_97 (not_97_out, OP2);
  not not_98 (not_98_out, OP1);
  not not_99 (not_99_out, OP0);
  not not_100 (not_100_out, F5);
  not not_101 (not_101_out, F4);
  not not_102 (not_102_out, F3);
  not not_103 (not_103_out, F2);
  not not_104 (not_104_out, F0);
  not not_105 (not_105_out, OP5);
  not not_106 (not_106_out, OP4);
  not not_107 (not_107_out, OP3);
  not not_108 (not_108_out, OP2);
  not not_109 (not_109_out, OP1);
  not not_110 (not_110_out, OP0);
  not not_111 (not_111_out, F4);
  not not_112 (not_112_out, F3);
  not not_113 (not_113_out, F2);
  not not_114 (not_114_out, F0);
  not not_115 (not_115_out, OP5);
  not not_116 (not_116_out, OP4);
  not not_117 (not_117_out, OP3);
  not not_118 (not_118_out, OP2);
  not not_119 (not_119_out, OP1);
  not not_120 (not_120_out, OP0);
  not not_121 (not_121_out, F4);
  not not_122 (not_122_out, F3);
  not not_123 (not_123_out, F1);
  not not_124 (not_124_out, F0);
  not not_125 (not_125_out, OP5);
  not not_126 (not_126_out, OP4);
  not not_127 (not_127_out, OP3);
  not not_128 (not_128_out, OP2);
  not not_129 (not_129_out, OP1);
  not not_130 (not_130_out, OP0);
  not not_131 (not_131_out, F4);
  not not_132 (not_132_out, F3);
  not not_133 (not_133_out, OP5);
  not not_134 (not_134_out, OP4);
  not not_135 (not_135_out, OP3);
  not not_136 (not_136_out, OP2);
  not not_137 (not_137_out, OP1);
  not not_138 (not_138_out, OP0);
  not not_139 (not_139_out, F4);
  not not_140 (not_140_out, F2);
  not not_141 (not_141_out, F0);
  not not_142 (not_142_out, OP5);
  not not_143 (not_143_out, OP4);
  not not_144 (not_144_out, OP3);
  not not_145 (not_145_out, OP1);
  not not_146 (not_146_out, OP0);
  not not_147 (not_147_out, OP5);
  not not_148 (not_148_out, OP4);
  not not_149 (not_149_out, OP3);
  not not_150 (not_150_out, OP1);
  not not_151 (not_151_out, OP5);
  not not_152 (not_152_out, OP4);
  not not_153 (not_153_out, OP1);
  not not_154 (not_154_out, OP0);
  not not_155 (not_155_out, OP5);
  not not_156 (not_156_out, OP4);
  not not_157 (not_157_out, OP2);
  not not_158 (not_158_out, OP0);
  not not_159 (not_159_out, OP5);
  not not_160 (not_160_out, OP4);
  not not_161 (not_161_out, OP3);
  not not_162 (not_162_out, OP2);
  not not_163 (not_163_out, OP1);
  not not_164 (not_164_out, OP0);
  not not_165 (not_165_out, F4);
  not not_166 (not_166_out, F3);
  not not_167 (not_167_out, F2);
  not not_168 (not_168_out, OP5);
  not not_169 (not_169_out, OP4);
  not not_170 (not_170_out, OP3);
  not not_171 (not_171_out, OP2);
  not not_172 (not_172_out, OP1);
  not not_173 (not_173_out, OP5);
  not not_174 (not_174_out, OP4);
  not not_175 (not_175_out, OP3);
  not not_176 (not_176_out, OP2);
  not not_177 (not_177_out, OP1);
  not not_178 (not_178_out, OP0);
  not not_179 (not_179_out, F4);
  not not_180 (not_180_out, F3);
  not not_181 (not_181_out, F2);
  not not_182 (not_182_out, F1);
  not not_183 (not_183_out, F0);
  not not_184 (not_184_out, OP5);
  not not_185 (not_185_out, OP4);
  not not_186 (not_186_out, OP3);
  not not_187 (not_187_out, OP2);
  not not_188 (not_188_out, OP1);
  not not_189 (not_189_out, OP0);
  not not_190 (not_190_out, F4);
  not not_191 (not_191_out, F3);
  not not_192 (not_192_out, F2);
  not not_193 (not_193_out, F1);
  not not_194 (not_194_out, OP5);
  not not_195 (not_195_out, OP4);
  not not_196 (not_196_out, OP3);
  not not_197 (not_197_out, OP2);
  not not_198 (not_198_out, OP1);
  not not_199 (not_199_out, OP0);
  not not_200 (not_200_out, F4);
  not not_201 (not_201_out, F3);
  not not_202 (not_202_out, F2);
  not not_203 (not_203_out, F0);
  not not_204 (not_204_out, OP5);
  not not_205 (not_205_out, OP4);
  not not_206 (not_206_out, OP3);
  not not_207 (not_207_out, OP2);
  not not_208 (not_208_out, OP1);
  not not_209 (not_209_out, OP0);
  not not_210 (not_210_out, F4);
  not not_211 (not_211_out, F3);
  not not_212 (not_212_out, F1);
  not not_213 (not_213_out, F0);
  not not_214 (not_214_out, OP5);
  not not_215 (not_215_out, OP4);
  not not_216 (not_216_out, OP3);
  not not_217 (not_217_out, OP2);
  not not_218 (not_218_out, OP1);
  not not_219 (not_219_out, OP0);
  not not_220 (not_220_out, F4);
  not not_221 (not_221_out, F2);
  not not_222 (not_222_out, OP5);
  not not_223 (not_223_out, OP4);
  not not_224 (not_224_out, OP2);
  not not_225 (not_225_out, OP1);
  not not_226 (not_226_out, OP0);
  not not_227 (not_227_out, OP5);
  not not_228 (not_228_out, OP4);
  not not_229 (not_229_out, OP1);
  not not_230 (not_230_out, OP0);
  not not_231 (not_231_out, OP5);
  not not_232 (not_232_out, OP4);
  not not_233 (not_233_out, OP2);
  not not_234 (not_234_out, OP1);
  not not_235 (not_235_out, OP4);
  not not_236 (not_236_out, OP3);
  not not_237 (not_237_out, OP2);
  not not_238 (not_238_out, OP4);
  not not_239 (not_239_out, OP2);
  not not_240 (not_240_out, OP5);
  not not_241 (not_241_out, OP4);
  not not_242 (not_242_out, OP3);
  not not_243 (not_243_out, OP2);
  not not_244 (not_244_out, OP1);
  not not_245 (not_245_out, OP0);
  not not_246 (not_246_out, F4);
  not not_247 (not_247_out, F3);
  not not_248 (not_248_out, F2);
  not not_249 (not_249_out, OP4);
  not not_250 (not_250_out, OP3);
  not not_251 (not_251_out, OP2);
  not not_252 (not_252_out, OP1);
  not not_253 (not_253_out, OP5);
  not not_254 (not_254_out, OP4);
  not not_255 (not_255_out, OP3);
  not not_256 (not_256_out, OP2);
  not not_257 (not_257_out, OP1);
  not not_258 (not_258_out, OP0);
  not not_259 (not_259_out, F4);
  not not_260 (not_260_out, F3);
  not not_261 (not_261_out, F1);
  not not_262 (not_262_out, OP5);
  not not_263 (not_263_out, OP4);
  not not_264 (not_264_out, OP3);
  not not_265 (not_265_out, OP2);
  not not_266 (not_266_out, OP1);
  not not_267 (not_267_out, OP0);
  not not_268 (not_268_out, F4);
  not not_269 (not_269_out, F3);
  not not_270 (not_270_out, OP5);
  not not_271 (not_271_out, OP4);
  not not_272 (not_272_out, OP3);
  not not_273 (not_273_out, OP2);
  not not_274 (not_274_out, OP1);
  not not_275 (not_275_out, OP0);
  not not_276 (not_276_out, F4);
  not not_277 (not_277_out, F2);
  not not_278 (not_278_out, F0);
  not not_279 (not_279_out, OP5);
  not not_280 (not_280_out, OP4);
  not not_281 (not_281_out, OP3);
  not not_282 (not_282_out, OP2);
  not not_283 (not_283_out, OP1);
  not not_284 (not_284_out, OP0);
  not not_285 (not_285_out, F4);
  not not_286 (not_286_out, F2);
  not not_287 (not_287_out, OP5);
  not not_288 (not_288_out, OP4);
  not not_289 (not_289_out, OP3);
  not not_290 (not_290_out, OP1);
  not not_291 (not_291_out, OP0);
  not not_292 (not_292_out, OP5);
  not not_293 (not_293_out, OP4);
  not not_294 (not_294_out, OP3);
  not not_295 (not_295_out, OP1);
  not not_296 (not_296_out, OP5);
  not not_297 (not_297_out, OP4);
  not not_298 (not_298_out, OP2);
  not not_299 (not_299_out, OP0);
  not not_300 (not_300_out, OP5);
  not not_301 (not_301_out, OP4);
  not not_302 (not_302_out, OP1);
  not not_303 (not_303_out, OP5);
  not not_304 (not_304_out, OP4);
  not not_305 (not_305_out, OP0);
  not not_306 (not_306_out, OP5);
  not not_307 (not_307_out, OP4);
  not not_308 (not_308_out, OP3);
  not not_309 (not_309_out, OP2);
  not not_310 (not_310_out, OP1);
  and and_1 (and_1_out, not_1_out, not_2_out, not_3_out, not_4_out, not_5_out, not_6_out, not_7_out, not_8_out, not_9_out, not_10_out, F1, F0);
  and and_2 (and_2_out, not_11_out, not_12_out, not_13_out, not_14_out, not_15_out, not_16_out, F5, not_17_out, not_18_out, not_19_out, not_20_out, not_21_out);
  and and_3 (and_3_out, not_22_out, not_23_out, not_24_out, not_25_out, not_26_out, not_27_out, F5, not_28_out, not_29_out, not_30_out, not_31_out, F0);
  and and_4 (and_4_out, not_32_out, not_33_out, not_34_out, not_35_out, not_36_out, not_37_out, F5, not_38_out, not_39_out, F2, not_40_out, not_41_out);
  and and_5 (and_5_out, not_42_out, not_43_out, not_44_out, not_45_out, not_46_out, not_47_out, F5, not_48_out, F3, not_49_out, F1, not_50_out);
  and and_6 (and_6_out, not_51_out, not_52_out, not_53_out, OP2, not_54_out, not_55_out);
  and and_7 (and_7_out, not_56_out, not_57_out, not_58_out, OP2, not_59_out, OP0);
  and and_8 (and_8_out, not_60_out, not_61_out, OP3, not_62_out, not_63_out, not_64_out);
  and and_9 (and_9_out, not_65_out, not_66_out, OP3, OP2, not_67_out, not_68_out);
  and and_10 (and_10_out, not_69_out, not_70_out, OP3, not_71_out, not_72_out, OP0);
  and and_11 (and_11_out, not_73_out, not_74_out, OP3, not_75_out, OP1, not_76_out);
  and and_12 (and_12_out, OP5, not_77_out, not_78_out, not_79_out, OP1, OP0);
  and and_13 (and_13_out, OP5, not_80_out, OP3, not_81_out, OP1, OP0);
  and and_14 (and_14_out, not_82_out, not_83_out, OP3, OP2, OP1, not_84_out);
  and and_15 (and_15_out, OP5, not_85_out, not_86_out, not_87_out, not_88_out, OP0);
  and and_16 (and_16_out, not_89_out, not_90_out, not_91_out, not_92_out, not_93_out, OP0);
  and and_17 (and_17_out, not_94_out, not_95_out, not_96_out, not_97_out, not_98_out, not_99_out, not_100_out, not_101_out, not_102_out, not_103_out, F1, not_104_out);
  and and_18 (and_18_out, not_105_out, not_106_out, not_107_out, not_108_out, not_109_out, not_110_out, F5, not_111_out, not_112_out, not_113_out, F1, not_114_out);
  and and_19 (and_19_out, not_115_out, not_116_out, not_117_out, not_118_out, not_119_out, not_120_out, F5, not_121_out, not_122_out, F2, not_123_out, not_124_out);
  and and_20 (and_20_out, not_125_out, not_126_out, not_127_out, not_128_out, not_129_out, not_130_out, F5, not_131_out, not_132_out, F2, F1, F0);
  and and_21 (and_21_out, not_133_out, not_134_out, not_135_out, not_136_out, not_137_out, not_138_out, F5, not_139_out, F3, not_140_out, F1, not_141_out);
  and and_22 (and_22_out, not_142_out, not_143_out, not_144_out, OP2, not_145_out, not_146_out);
  and and_23 (and_23_out, not_147_out, not_148_out, not_149_out, OP2, not_150_out, OP0);
  and and_24 (and_24_out, not_151_out, not_152_out, OP3, OP2, not_153_out, not_154_out);
  and and_25 (and_25_out, not_155_out, not_156_out, OP3, not_157_out, OP1, not_158_out);
  and and_26 (and_26_out, not_159_out, not_160_out, not_161_out, not_162_out, not_163_out, not_164_out, F5, not_165_out, not_166_out, not_167_out, F1, F0);
  and and_27 (and_27_out, not_168_out, not_169_out, not_170_out, not_171_out, not_172_out, OP0);
  and and_28 (and_28_out, not_173_out, not_174_out, not_175_out, not_176_out, not_177_out, not_178_out, F5, not_179_out, not_180_out, not_181_out, not_182_out, not_183_out);
  and and_29 (and_29_out, not_184_out, not_185_out, not_186_out, not_187_out, not_188_out, not_189_out, F5, not_190_out, not_191_out, not_192_out, not_193_out, F0);
  and and_30 (and_30_out, not_194_out, not_195_out, not_196_out, not_197_out, not_198_out, not_199_out, F5, not_200_out, not_201_out, not_202_out, F1, not_203_out);
  and and_31 (and_31_out, not_204_out, not_205_out, not_206_out, not_207_out, not_208_out, not_209_out, F5, not_210_out, not_211_out, F2, not_212_out, not_213_out);
  and and_32 (and_32_out, not_214_out, not_215_out, not_216_out, not_217_out, not_218_out, not_219_out, F5, not_220_out, F3, not_221_out, F1, F0);
  and and_33 (and_33_out, not_222_out, not_223_out, OP3, not_224_out, not_225_out, not_226_out);
  and and_34 (and_34_out, not_227_out, not_228_out, OP3, OP2, not_229_out, not_230_out);
  and and_35 (and_35_out, not_231_out, not_232_out, OP3, not_233_out, not_234_out, OP0);
  and and_36 (and_36_out, OP5, not_235_out, not_236_out, not_237_out, OP1, OP0);
  and and_37 (and_37_out, OP5, not_238_out, OP3, not_239_out, OP1, OP0);
  and and_38 (and_38_out, not_240_out, not_241_out, not_242_out, not_243_out, not_244_out, not_245_out, F5, not_246_out, not_247_out, not_248_out, F1, F0);
  and and_39 (and_39_out, OP5, not_249_out, not_250_out, not_251_out, not_252_out, OP0);
  and and_40 (and_40_out, not_253_out, not_254_out, not_255_out, not_256_out, not_257_out, not_258_out, F5, not_259_out, not_260_out, F2, not_261_out, F0);
  and and_41 (and_41_out, not_262_out, not_263_out, not_264_out, not_265_out, not_266_out, not_267_out, F5, not_268_out, not_269_out, F2, F1, F0);
  and and_42 (and_42_out, not_270_out, not_271_out, not_272_out, not_273_out, not_274_out, not_275_out, F5, not_276_out, F3, not_277_out, F1, not_278_out);
  and and_43 (and_43_out, not_279_out, not_280_out, not_281_out, not_282_out, not_283_out, not_284_out, F5, not_285_out, F3, not_286_out, F1, F0);
  and and_44 (and_44_out, not_287_out, not_288_out, not_289_out, OP2, not_290_out, not_291_out);
  and and_45 (and_45_out, not_292_out, not_293_out, not_294_out, OP2, not_295_out, OP0);
  and and_46 (and_46_out, not_296_out, not_297_out, OP3, not_298_out, OP1, not_299_out);
  and and_47 (and_47_out, not_300_out, not_301_out, OP3, OP2, not_302_out, OP0);
  and and_48 (and_48_out, not_303_out, not_304_out, OP3, OP2, OP1, not_305_out);
  and and_49 (and_49_out, not_306_out, not_307_out, not_308_out, not_309_out, not_310_out, OP0);
  or or_1 (S1, and_17_out, and_18_out, and_19_out, and_20_out, and_21_out, and_22_out, and_23_out, and_24_out, and_25_out, and_26_out, and_27_out);
  or or_2 (S3, and_40_out, and_41_out, and_42_out, and_43_out, and_44_out, and_45_out, and_46_out, and_47_out, and_48_out, and_49_out);
  or or_3 (S0, and_1_out, and_2_out, and_3_out, and_4_out, and_5_out, and_6_out, and_7_out, and_8_out, and_9_out, and_10_out, and_11_out, and_12_out, and_13_out, and_14_out, and_15_out, and_16_out);
  or or_4 (S2, and_28_out, and_29_out, and_30_out, and_31_out, and_32_out, and_33_out, and_34_out, and_35_out, and_36_out, and_37_out, and_38_out, and_39_out);
endmodule

// 控制信号生成
module \控制信号生成  (
  input  OP0,
  input  OP1,
  input  OP2,
  input  OP3,
  input  OP4,
  input  OP5,
  input  F0,
  input  F1,
  input  F2,
  input  F3,
  input  F4,
  input  F5,
  output MemWrite,
  output JAL,
  output JMP,
  output ALU_SRC,
  output RegWrite,
  output SysCALL,
  output MemtoReg,
  output SignedExt,
  output RegDst,
  output BEQ,
  output BNE,
  output JR,
  output BGEZ
);

  wire and_4_out, and_5_out, and_6_out, and_7_out, and_8_out, and_9_out, and_10_out, and_11_out, and_12_out,
       and_13_out, and_14_out, and_15_out, and_16_out, and_17_out, and_18_out, and_19_out, and_20_out,
       and_21_out, and_22_out, and_23_out, and_24_out, and_25_out, and_26_out, and_27_out, and_28_out,
       and_29_out, and_30_out, and_31_out, and_32_out, and_33_out, and_35_out, and_36_out, and_37_out,
       and_38_out, and_39_out, and_40_out, and_41_out, and_42_out, and_43_out, and_44_out, and_45_out,
       and_46_out, and_47_out, and_48_out, and_49_out, and_50_out, and_51_out, and_52_out, and_53_out,
       and_54_out, and_55_out, and_56_out, not_1_out, not_2_out, not_3_out, not_4_out, not_5_out, not_6_out,
       not_7_out, not_8_out, not_9_out, not_10_out, not_11_out, not_12_out, not_13_out, not_14_out,
       not_15_out, not_16_out, not_17_out, not_18_out, not_19_out, not_20_out, not_21_out, not_22_out,
       not_23_out, not_24_out, not_25_out, not_26_out, not_27_out, not_28_out, not_29_out, not_30_out,
       not_31_out, not_32_out, not_33_out, not_34_out, not_35_out, not_36_out, not_37_out, not_38_out,
       not_39_out, not_40_out, not_41_out, not_42_out, not_43_out, not_44_out, not_45_out, not_46_out,
       not_47_out, not_48_out, not_49_out, not_50_out, not_51_out, not_52_out, not_53_out, not_54_out,
       not_55_out, not_56_out, not_57_out, not_58_out, not_59_out, not_60_out, not_61_out, not_62_out,
       not_63_out, not_64_out, not_65_out, not_66_out, not_67_out, not_68_out, not_69_out, not_70_out,
       not_71_out, not_72_out, not_73_out, not_74_out, not_75_out, not_76_out, not_77_out, not_78_out,
       not_79_out, not_80_out, not_81_out, not_82_out, not_83_out, not_84_out, not_85_out, not_86_out,
       not_87_out, not_88_out, not_89_out, not_90_out, not_91_out, not_92_out, not_93_out, not_94_out,
       not_95_out, not_96_out, not_97_out, not_98_out, not_99_out, not_100_out, not_101_out, not_102_out,
       not_103_out, not_104_out, not_105_out, not_106_out, not_107_out, not_108_out, not_109_out,
       not_110_out, not_111_out, not_112_out, not_113_out, not_114_out, not_115_out, not_116_out,
       not_117_out, not_118_out, not_119_out, not_120_out, not_121_out, not_122_out, not_123_out,
       not_124_out, not_125_out, not_126_out, not_127_out, not_128_out, not_129_out, not_130_out,
       not_131_out, not_132_out, not_133_out, not_134_out, not_135_out, not_136_out, not_137_out,
       not_138_out, not_139_out, not_140_out, not_141_out, not_142_out, not_143_out, not_144_out,
       not_145_out, not_146_out, not_147_out, not_148_out, not_149_out, not_150_out, not_151_out,
       not_152_out, not_153_out, not_154_out, not_155_out, not_156_out, not_157_out, not_158_out,
       not_159_out, not_160_out, not_161_out, not_162_out, not_163_out, not_164_out, not_165_out,
       not_166_out, not_167_out, not_168_out, not_169_out, not_170_out, not_171_out, not_172_out,
       not_173_out, not_174_out, not_175_out, not_176_out, not_177_out, not_178_out, not_179_out,
       not_180_out, not_181_out, not_182_out, not_183_out, not_184_out, not_185_out, not_186_out,
       not_187_out, not_188_out, not_189_out, not_190_out, not_191_out, not_192_out, not_193_out,
       not_194_out, not_195_out, not_196_out, not_197_out, not_198_out, not_199_out, not_200_out,
       not_201_out, not_202_out, not_203_out, not_204_out, not_205_out, not_206_out, not_207_out,
       not_208_out, not_209_out, not_210_out, not_211_out, not_212_out, not_213_out, not_214_out,
       not_215_out, not_216_out, not_217_out, not_218_out, not_219_out, not_220_out, not_221_out,
       not_222_out, not_223_out, not_224_out, not_225_out, not_226_out, not_227_out, not_228_out,
       not_229_out, not_230_out, not_231_out, not_232_out, not_233_out, not_234_out, not_235_out,
       not_236_out, not_237_out, not_238_out, not_239_out, not_240_out, not_241_out, not_242_out,
       not_243_out, not_244_out, not_245_out, not_246_out, not_247_out, not_248_out, not_249_out,
       not_250_out, not_251_out, not_252_out, not_253_out, not_254_out, not_255_out, not_256_out,
       not_257_out, not_258_out, not_259_out, not_260_out, not_261_out, not_262_out, not_263_out,
       not_264_out, not_265_out, not_266_out, not_267_out, not_268_out, not_269_out, not_270_out,
       not_271_out, not_272_out, not_273_out, not_274_out, not_275_out, not_276_out, not_277_out,
       not_278_out, not_279_out, not_280_out, not_281_out, not_282_out, not_283_out, not_284_out,
       not_285_out, not_286_out, not_287_out, not_288_out, not_289_out, not_290_out, not_291_out,
       not_292_out, not_293_out, not_294_out, not_295_out, not_296_out, not_297_out, not_298_out,
       not_299_out, not_300_out, not_301_out, not_302_out, not_303_out, not_304_out, not_305_out,
       not_306_out, not_307_out, not_308_out, not_309_out, not_310_out, not_311_out, not_312_out,
       not_313_out, not_314_out, not_315_out, not_316_out, not_317_out, not_318_out, not_319_out,
       not_320_out, not_321_out, not_322_out, not_323_out, not_324_out, not_325_out, not_326_out,
       not_327_out, not_328_out, not_329_out, not_330_out, not_331_out, not_332_out, not_333_out,
       not_334_out, not_335_out, not_336_out, not_337_out, not_338_out, not_339_out, not_340_out,
       not_341_out, not_342_out, not_343_out, not_344_out, not_345_out, not_346_out, not_347_out,
       not_348_out, not_349_out, not_350_out, not_351_out, not_352_out, not_353_out, not_354_out,
       not_355_out, not_356_out, not_357_out, not_358_out, not_359_out, not_360_out, not_361_out,
       not_362_out, not_363_out, not_364_out, not_365_out, not_366_out, not_367_out, not_368_out,
       not_369_out, not_370_out, not_371_out, not_372_out, not_373_out, not_374_out, not_375_out,
       not_376_out, not_377_out, not_378_out, not_379_out, not_380_out, not_381_out, not_382_out,
       not_383_out, not_384_out, not_385_out;

  not not_1 (not_1_out, OP4);
  not not_2 (not_2_out, OP2);
  not not_3 (not_3_out, OP5);
  not not_4 (not_4_out, OP4);
  not not_5 (not_5_out, OP3);
  not not_6 (not_6_out, OP2);
  not not_7 (not_7_out, OP5);
  not not_8 (not_8_out, OP4);
  not not_9 (not_9_out, OP3);
  not not_10 (not_10_out, OP2);
  not not_11 (not_11_out, OP0);
  not not_12 (not_12_out, OP5);
  not not_13 (not_13_out, OP4);
  not not_14 (not_14_out, OP2);
  not not_15 (not_15_out, OP1);
  not not_16 (not_16_out, OP0);
  not not_17 (not_17_out, OP5);
  not not_18 (not_18_out, OP4);
  not not_19 (not_19_out, OP1);
  not not_20 (not_20_out, OP0);
  not not_21 (not_21_out, OP5);
  not not_22 (not_22_out, OP4);
  not not_23 (not_23_out, OP2);
  not not_24 (not_24_out, OP1);
  not not_25 (not_25_out, OP5);
  not not_26 (not_26_out, OP4);
  not not_27 (not_27_out, OP2);
  not not_28 (not_28_out, OP0);
  not not_29 (not_29_out, OP5);
  not not_30 (not_30_out, OP4);
  not not_31 (not_31_out, OP1);
  not not_32 (not_32_out, OP4);
  not not_33 (not_33_out, OP3);
  not not_34 (not_34_out, OP2);
  not not_35 (not_35_out, OP4);
  not not_36 (not_36_out, OP2);
  not not_37 (not_37_out, OP5);
  not not_38 (not_38_out, OP4);
  not not_39 (not_39_out, OP0);
  not not_40 (not_40_out, OP4);
  not not_41 (not_41_out, OP3);
  not not_42 (not_42_out, OP2);
  not not_43 (not_43_out, OP1);
  not not_44 (not_44_out, OP5);
  not not_45 (not_45_out, OP4);
  not not_46 (not_46_out, OP3);
  not not_47 (not_47_out, OP2);
  not not_48 (not_48_out, OP1);
  not not_49 (not_49_out, OP0);
  not not_50 (not_50_out, F5);
  not not_51 (not_51_out, F4);
  not not_52 (not_52_out, F3);
  not not_53 (not_53_out, F2);
  not not_54 (not_54_out, F1);
  not not_55 (not_55_out, F0);
  not not_56 (not_56_out, OP5);
  not not_57 (not_57_out, OP4);
  not not_58 (not_58_out, OP3);
  not not_59 (not_59_out, OP2);
  not not_60 (not_60_out, OP1);
  not not_61 (not_61_out, OP0);
  not not_62 (not_62_out, F5);
  not not_63 (not_63_out, F4);
  not not_64 (not_64_out, F3);
  not not_65 (not_65_out, F2);
  not not_66 (not_66_out, OP5);
  not not_67 (not_67_out, OP4);
  not not_68 (not_68_out, OP3);
  not not_69 (not_69_out, OP2);
  not not_70 (not_70_out, OP1);
  not not_71 (not_71_out, OP0);
  not not_72 (not_72_out, F5);
  not not_73 (not_73_out, F4);
  not not_74 (not_74_out, F3);
  not not_75 (not_75_out, F2);
  not not_76 (not_76_out, F0);
  not not_77 (not_77_out, OP5);
  not not_78 (not_78_out, OP4);
  not not_79 (not_79_out, OP3);
  not not_80 (not_80_out, OP2);
  not not_81 (not_81_out, OP1);
  not not_82 (not_82_out, OP0);
  not not_83 (not_83_out, F4);
  not not_84 (not_84_out, F3);
  not not_85 (not_85_out, F2);
  not not_86 (not_86_out, F1);
  not not_87 (not_87_out, F0);
  not not_88 (not_88_out, OP5);
  not not_89 (not_89_out, OP4);
  not not_90 (not_90_out, OP3);
  not not_91 (not_91_out, OP2);
  not not_92 (not_92_out, OP1);
  not not_93 (not_93_out, OP0);
  not not_94 (not_94_out, F4);
  not not_95 (not_95_out, F3);
  not not_96 (not_96_out, F2);
  not not_97 (not_97_out, F1);
  not not_98 (not_98_out, OP5);
  not not_99 (not_99_out, OP4);
  not not_100 (not_100_out, OP3);
  not not_101 (not_101_out, OP2);
  not not_102 (not_102_out, OP1);
  not not_103 (not_103_out, OP0);
  not not_104 (not_104_out, F4);
  not not_105 (not_105_out, F3);
  not not_106 (not_106_out, F2);
  not not_107 (not_107_out, F0);
  not not_108 (not_108_out, OP5);
  not not_109 (not_109_out, OP4);
  not not_110 (not_110_out, OP3);
  not not_111 (not_111_out, OP2);
  not not_112 (not_112_out, OP1);
  not not_113 (not_113_out, OP0);
  not not_114 (not_114_out, F4);
  not not_115 (not_115_out, F3);
  not not_116 (not_116_out, F1);
  not not_117 (not_117_out, F0);
  not not_118 (not_118_out, OP5);
  not not_119 (not_119_out, OP4);
  not not_120 (not_120_out, OP3);
  not not_121 (not_121_out, OP2);
  not not_122 (not_122_out, OP1);
  not not_123 (not_123_out, OP0);
  not not_124 (not_124_out, F4);
  not not_125 (not_125_out, F3);
  not not_126 (not_126_out, F1);
  not not_127 (not_127_out, OP5);
  not not_128 (not_128_out, OP4);
  not not_129 (not_129_out, OP3);
  not not_130 (not_130_out, OP2);
  not not_131 (not_131_out, OP1);
  not not_132 (not_132_out, OP0);
  not not_133 (not_133_out, F4);
  not not_134 (not_134_out, F3);
  not not_135 (not_135_out, OP5);
  not not_136 (not_136_out, OP4);
  not not_137 (not_137_out, OP3);
  not not_138 (not_138_out, OP2);
  not not_139 (not_139_out, OP1);
  not not_140 (not_140_out, OP0);
  not not_141 (not_141_out, F4);
  not not_142 (not_142_out, F2);
  not not_143 (not_143_out, F0);
  not not_144 (not_144_out, OP5);
  not not_145 (not_145_out, OP4);
  not not_146 (not_146_out, OP3);
  not not_147 (not_147_out, OP2);
  not not_148 (not_148_out, OP1);
  not not_149 (not_149_out, OP0);
  not not_150 (not_150_out, F4);
  not not_151 (not_151_out, F2);
  not not_152 (not_152_out, OP5);
  not not_153 (not_153_out, OP4);
  not not_154 (not_154_out, OP3);
  not not_155 (not_155_out, OP2);
  not not_156 (not_156_out, OP5);
  not not_157 (not_157_out, OP4);
  not not_158 (not_158_out, OP2);
  not not_159 (not_159_out, OP1);
  not not_160 (not_160_out, OP0);
  not not_161 (not_161_out, OP5);
  not not_162 (not_162_out, OP4);
  not not_163 (not_163_out, OP1);
  not not_164 (not_164_out, OP0);
  not not_165 (not_165_out, OP5);
  not not_166 (not_166_out, OP4);
  not not_167 (not_167_out, OP2);
  not not_168 (not_168_out, OP1);
  not not_169 (not_169_out, OP5);
  not not_170 (not_170_out, OP4);
  not not_171 (not_171_out, OP2);
  not not_172 (not_172_out, OP0);
  not not_173 (not_173_out, OP5);
  not not_174 (not_174_out, OP4);
  not not_175 (not_175_out, OP1);
  not not_176 (not_176_out, OP4);
  not not_177 (not_177_out, OP3);
  not not_178 (not_178_out, OP2);
  not not_179 (not_179_out, OP5);
  not not_180 (not_180_out, OP4);
  not not_181 (not_181_out, OP3);
  not not_182 (not_182_out, OP2);
  not not_183 (not_183_out, OP1);
  not not_184 (not_184_out, OP0);
  not not_185 (not_185_out, F4);
  not not_186 (not_186_out, F3);
  not not_187 (not_187_out, F2);
  not not_188 (not_188_out, OP5);
  not not_189 (not_189_out, OP4);
  not not_190 (not_190_out, OP0);
  not not_191 (not_191_out, OP4);
  not not_192 (not_192_out, OP3);
  not not_193 (not_193_out, OP2);
  not not_194 (not_194_out, OP1);
  not not_195 (not_195_out, OP5);
  not not_196 (not_196_out, OP4);
  not not_197 (not_197_out, OP3);
  not not_198 (not_198_out, OP2);
  not not_199 (not_199_out, OP1);
  not not_200 (not_200_out, OP0);
  not not_201 (not_201_out, F5);
  not not_202 (not_202_out, F4);
  not not_203 (not_203_out, F1);
  not not_204 (not_204_out, F0);
  not not_205 (not_205_out, OP4);
  not not_206 (not_206_out, OP3);
  not not_207 (not_207_out, OP2);
  not not_208 (not_208_out, OP4);
  not not_209 (not_209_out, OP3);
  not not_210 (not_210_out, OP2);
  not not_211 (not_211_out, OP1);
  not not_212 (not_212_out, OP5);
  not not_213 (not_213_out, OP4);
  not not_214 (not_214_out, OP3);
  not not_215 (not_215_out, OP1);
  not not_216 (not_216_out, OP0);
  not not_217 (not_217_out, OP5);
  not not_218 (not_218_out, OP4);
  not not_219 (not_219_out, OP3);
  not not_220 (not_220_out, OP1);
  not not_221 (not_221_out, OP5);
  not not_222 (not_222_out, OP4);
  not not_223 (not_223_out, OP2);
  not not_224 (not_224_out, OP1);
  not not_225 (not_225_out, OP0);
  not not_226 (not_226_out, OP5);
  not not_227 (not_227_out, OP4);
  not not_228 (not_228_out, OP2);
  not not_229 (not_229_out, OP0);
  not not_230 (not_230_out, OP4);
  not not_231 (not_231_out, OP3);
  not not_232 (not_232_out, OP2);
  not not_233 (not_233_out, OP4);
  not not_234 (not_234_out, OP2);
  not not_235 (not_235_out, OP4);
  not not_236 (not_236_out, OP3);
  not not_237 (not_237_out, OP2);
  not not_238 (not_238_out, OP1);
  not not_239 (not_239_out, OP5);
  not not_240 (not_240_out, OP4);
  not not_241 (not_241_out, OP3);
  not not_242 (not_242_out, OP2);
  not not_243 (not_243_out, OP1);
  not not_244 (not_244_out, OP5);
  not not_245 (not_245_out, OP4);
  not not_246 (not_246_out, OP3);
  not not_247 (not_247_out, OP2);
  not not_248 (not_248_out, OP1);
  not not_249 (not_249_out, OP0);
  not not_250 (not_250_out, F5);
  not not_251 (not_251_out, F4);
  not not_252 (not_252_out, F3);
  not not_253 (not_253_out, F2);
  not not_254 (not_254_out, F1);
  not not_255 (not_255_out, F0);
  not not_256 (not_256_out, OP5);
  not not_257 (not_257_out, OP4);
  not not_258 (not_258_out, OP3);
  not not_259 (not_259_out, OP2);
  not not_260 (not_260_out, OP1);
  not not_261 (not_261_out, OP0);
  not not_262 (not_262_out, F5);
  not not_263 (not_263_out, F4);
  not not_264 (not_264_out, F3);
  not not_265 (not_265_out, F2);
  not not_266 (not_266_out, OP5);
  not not_267 (not_267_out, OP4);
  not not_268 (not_268_out, OP3);
  not not_269 (not_269_out, OP2);
  not not_270 (not_270_out, OP1);
  not not_271 (not_271_out, OP0);
  not not_272 (not_272_out, F5);
  not not_273 (not_273_out, F4);
  not not_274 (not_274_out, F3);
  not not_275 (not_275_out, F2);
  not not_276 (not_276_out, F0);
  not not_277 (not_277_out, OP5);
  not not_278 (not_278_out, OP4);
  not not_279 (not_279_out, OP3);
  not not_280 (not_280_out, OP2);
  not not_281 (not_281_out, OP1);
  not not_282 (not_282_out, OP0);
  not not_283 (not_283_out, F4);
  not not_284 (not_284_out, F3);
  not not_285 (not_285_out, F2);
  not not_286 (not_286_out, F1);
  not not_287 (not_287_out, F0);
  not not_288 (not_288_out, OP5);
  not not_289 (not_289_out, OP4);
  not not_290 (not_290_out, OP3);
  not not_291 (not_291_out, OP2);
  not not_292 (not_292_out, OP1);
  not not_293 (not_293_out, OP0);
  not not_294 (not_294_out, F4);
  not not_295 (not_295_out, F3);
  not not_296 (not_296_out, F2);
  not not_297 (not_297_out, F1);
  not not_298 (not_298_out, OP5);
  not not_299 (not_299_out, OP4);
  not not_300 (not_300_out, OP3);
  not not_301 (not_301_out, OP2);
  not not_302 (not_302_out, OP1);
  not not_303 (not_303_out, OP0);
  not not_304 (not_304_out, F4);
  not not_305 (not_305_out, F3);
  not not_306 (not_306_out, F2);
  not not_307 (not_307_out, F0);
  not not_308 (not_308_out, OP5);
  not not_309 (not_309_out, OP4);
  not not_310 (not_310_out, OP3);
  not not_311 (not_311_out, OP2);
  not not_312 (not_312_out, OP1);
  not not_313 (not_313_out, OP0);
  not not_314 (not_314_out, F4);
  not not_315 (not_315_out, F3);
  not not_316 (not_316_out, F1);
  not not_317 (not_317_out, F0);
  not not_318 (not_318_out, OP5);
  not not_319 (not_319_out, OP4);
  not not_320 (not_320_out, OP3);
  not not_321 (not_321_out, OP2);
  not not_322 (not_322_out, OP1);
  not not_323 (not_323_out, OP0);
  not not_324 (not_324_out, F4);
  not not_325 (not_325_out, F3);
  not not_326 (not_326_out, F1);
  not not_327 (not_327_out, OP5);
  not not_328 (not_328_out, OP4);
  not not_329 (not_329_out, OP3);
  not not_330 (not_330_out, OP2);
  not not_331 (not_331_out, OP1);
  not not_332 (not_332_out, OP0);
  not not_333 (not_333_out, F4);
  not not_334 (not_334_out, F3);
  not not_335 (not_335_out, OP5);
  not not_336 (not_336_out, OP4);
  not not_337 (not_337_out, OP3);
  not not_338 (not_338_out, OP2);
  not not_339 (not_339_out, OP1);
  not not_340 (not_340_out, OP0);
  not not_341 (not_341_out, F4);
  not not_342 (not_342_out, F2);
  not not_343 (not_343_out, F0);
  not not_344 (not_344_out, OP5);
  not not_345 (not_345_out, OP4);
  not not_346 (not_346_out, OP3);
  not not_347 (not_347_out, OP2);
  not not_348 (not_348_out, OP1);
  not not_349 (not_349_out, OP0);
  not not_350 (not_350_out, F4);
  not not_351 (not_351_out, F2);
  not not_352 (not_352_out, OP5);
  not not_353 (not_353_out, OP4);
  not not_354 (not_354_out, OP3);
  not not_355 (not_355_out, OP2);
  not not_356 (not_356_out, OP1);
  not not_357 (not_357_out, OP0);
  not not_358 (not_358_out, F4);
  not not_359 (not_359_out, F3);
  not not_360 (not_360_out, F2);
  not not_361 (not_361_out, OP5);
  not not_362 (not_362_out, OP4);
  not not_363 (not_363_out, OP3);
  not not_364 (not_364_out, OP1);
  not not_365 (not_365_out, OP0);
  not not_366 (not_366_out, OP5);
  not not_367 (not_367_out, OP4);
  not not_368 (not_368_out, OP3);
  not not_369 (not_369_out, OP1);
  not not_370 (not_370_out, OP5);
  not not_371 (not_371_out, OP4);
  not not_372 (not_372_out, OP3);
  not not_373 (not_373_out, OP2);
  not not_374 (not_374_out, OP1);
  not not_375 (not_375_out, OP0);
  not not_376 (not_376_out, F5);
  not not_377 (not_377_out, F4);
  not not_378 (not_378_out, F2);
  not not_379 (not_379_out, F1);
  not not_380 (not_380_out, F0);
  not not_381 (not_381_out, OP5);
  not not_382 (not_382_out, OP4);
  not not_383 (not_383_out, OP3);
  not not_384 (not_384_out, OP2);
  not not_385 (not_385_out, OP1);
  and and_1 (MemWrite, OP5, not_1_out, OP3, not_2_out, OP1, OP0);
  and and_2 (JAL, not_3_out, not_4_out, not_5_out, not_6_out, OP1, OP0);
  and and_3 (JMP, not_7_out, not_8_out, not_9_out, not_10_out, OP1, not_11_out);
  and and_4 (and_4_out, not_12_out, not_13_out, OP3, not_14_out, not_15_out, not_16_out);
  and and_5 (and_5_out, not_17_out, not_18_out, OP3, OP2, not_19_out, not_20_out);
  and and_6 (and_6_out, not_21_out, not_22_out, OP3, not_23_out, not_24_out, OP0);
  and and_7 (and_7_out, not_25_out, not_26_out, OP3, not_27_out, OP1, not_28_out);
  and and_8 (and_8_out, not_29_out, not_30_out, OP3, OP2, not_31_out, OP0);
  and and_9 (and_9_out, OP5, not_32_out, not_33_out, not_34_out, OP1, OP0);
  and and_10 (and_10_out, OP5, not_35_out, OP3, not_36_out, OP1, OP0);
  and and_11 (and_11_out, not_37_out, not_38_out, OP3, OP2, OP1, not_39_out);
  and and_12 (and_12_out, OP5, not_40_out, not_41_out, not_42_out, not_43_out, OP0);
  and and_13 (and_13_out, not_44_out, not_45_out, not_46_out, not_47_out, not_48_out, not_49_out, not_50_out, not_51_out, not_52_out, not_53_out, not_54_out, not_55_out);
  and and_14 (and_14_out, not_56_out, not_57_out, not_58_out, not_59_out, not_60_out, not_61_out, not_62_out, not_63_out, not_64_out, not_65_out, F1, F0);
  and and_15 (and_15_out, not_66_out, not_67_out, not_68_out, not_69_out, not_70_out, not_71_out, not_72_out, not_73_out, not_74_out, not_75_out, F1, not_76_out);
  and and_16 (and_16_out, not_77_out, not_78_out, not_79_out, not_80_out, not_81_out, not_82_out, F5, not_83_out, not_84_out, not_85_out, not_86_out, not_87_out);
  and and_17 (and_17_out, not_88_out, not_89_out, not_90_out, not_91_out, not_92_out, not_93_out, F5, not_94_out, not_95_out, not_96_out, not_97_out, F0);
  and and_18 (and_18_out, not_98_out, not_99_out, not_100_out, not_101_out, not_102_out, not_103_out, F5, not_104_out, not_105_out, not_106_out, F1, not_107_out);
  and and_19 (and_19_out, not_108_out, not_109_out, not_110_out, not_111_out, not_112_out, not_113_out, F5, not_114_out, not_115_out, F2, not_116_out, not_117_out);
  and and_20 (and_20_out, not_118_out, not_119_out, not_120_out, not_121_out, not_122_out, not_123_out, F5, not_124_out, not_125_out, F2, not_126_out, F0);
  and and_21 (and_21_out, not_127_out, not_128_out, not_129_out, not_130_out, not_131_out, not_132_out, F5, not_133_out, not_134_out, F2, F1, F0);
  and and_22 (and_22_out, not_135_out, not_136_out, not_137_out, not_138_out, not_139_out, not_140_out, F5, not_141_out, F3, not_142_out, F1, not_143_out);
  and and_23 (and_23_out, not_144_out, not_145_out, not_146_out, not_147_out, not_148_out, not_149_out, F5, not_150_out, F3, not_151_out, F1, F0);
  and and_24 (and_24_out, not_152_out, not_153_out, not_154_out, not_155_out, OP1, OP0);
  and and_25 (and_25_out, not_156_out, not_157_out, OP3, not_158_out, not_159_out, not_160_out);
  and and_26 (and_26_out, not_161_out, not_162_out, OP3, OP2, not_163_out, not_164_out);
  and and_27 (and_27_out, not_165_out, not_166_out, OP3, not_167_out, not_168_out, OP0);
  and and_28 (and_28_out, not_169_out, not_170_out, OP3, not_171_out, OP1, not_172_out);
  and and_29 (and_29_out, not_173_out, not_174_out, OP3, OP2, not_175_out, OP0);
  and and_30 (and_30_out, OP5, not_176_out, not_177_out, not_178_out, OP1, OP0);
  and and_31 (and_31_out, not_179_out, not_180_out, not_181_out, not_182_out, not_183_out, not_184_out, F5, not_185_out, not_186_out, not_187_out, F1, F0);
  and and_32 (and_32_out, not_188_out, not_189_out, OP3, OP2, OP1, not_190_out);
  and and_33 (and_33_out, OP5, not_191_out, not_192_out, not_193_out, not_194_out, OP0);
  and and_34 (SysCALL, not_195_out, not_196_out, not_197_out, not_198_out, not_199_out, not_200_out, not_201_out, not_202_out, F3, F2, not_203_out, not_204_out);
  and and_35 (and_35_out, OP5, not_205_out, not_206_out, not_207_out, OP1, OP0);
  and and_36 (and_36_out, OP5, not_208_out, not_209_out, not_210_out, not_211_out, OP0);
  and and_37 (and_37_out, not_212_out, not_213_out, not_214_out, OP2, not_215_out, not_216_out);
  and and_38 (and_38_out, not_217_out, not_218_out, not_219_out, OP2, not_220_out, OP0);
  and and_39 (and_39_out, not_221_out, not_222_out, OP3, not_223_out, not_224_out, not_225_out);
  and and_40 (and_40_out, not_226_out, not_227_out, OP3, not_228_out, OP1, not_229_out);
  and and_41 (and_41_out, OP5, not_230_out, not_231_out, not_232_out, OP1, OP0);
  and and_42 (and_42_out, OP5, not_233_out, OP3, not_234_out, OP1, OP0);
  and and_43 (and_43_out, OP5, not_235_out, not_236_out, not_237_out, not_238_out, OP0);
  and and_44 (and_44_out, not_239_out, not_240_out, not_241_out, not_242_out, not_243_out, OP0);
  and and_45 (and_45_out, not_244_out, not_245_out, not_246_out, not_247_out, not_248_out, not_249_out, not_250_out, not_251_out, not_252_out, not_253_out, not_254_out, not_255_out);
  and and_46 (and_46_out, not_256_out, not_257_out, not_258_out, not_259_out, not_260_out, not_261_out, not_262_out, not_263_out, not_264_out, not_265_out, F1, F0);
  and and_47 (and_47_out, not_266_out, not_267_out, not_268_out, not_269_out, not_270_out, not_271_out, not_272_out, not_273_out, not_274_out, not_275_out, F1, not_276_out);
  and and_48 (and_48_out, not_277_out, not_278_out, not_279_out, not_280_out, not_281_out, not_282_out, F5, not_283_out, not_284_out, not_285_out, not_286_out, not_287_out);
  and and_49 (and_49_out, not_288_out, not_289_out, not_290_out, not_291_out, not_292_out, not_293_out, F5, not_294_out, not_295_out, not_296_out, not_297_out, F0);
  and and_50 (and_50_out, not_298_out, not_299_out, not_300_out, not_301_out, not_302_out, not_303_out, F5, not_304_out, not_305_out, not_306_out, F1, not_307_out);
  and and_51 (and_51_out, not_308_out, not_309_out, not_310_out, not_311_out, not_312_out, not_313_out, F5, not_314_out, not_315_out, F2, not_316_out, not_317_out);
  and and_52 (and_52_out, not_318_out, not_319_out, not_320_out, not_321_out, not_322_out, not_323_out, F5, not_324_out, not_325_out, F2, not_326_out, F0);
  and and_53 (and_53_out, not_327_out, not_328_out, not_329_out, not_330_out, not_331_out, not_332_out, F5, not_333_out, not_334_out, F2, F1, F0);
  and and_54 (and_54_out, not_335_out, not_336_out, not_337_out, not_338_out, not_339_out, not_340_out, F5, not_341_out, F3, not_342_out, F1, not_343_out);
  and and_55 (and_55_out, not_344_out, not_345_out, not_346_out, not_347_out, not_348_out, not_349_out, F5, not_350_out, F3, not_351_out, F1, F0);
  and and_56 (and_56_out, not_352_out, not_353_out, not_354_out, not_355_out, not_356_out, not_357_out, F5, not_358_out, not_359_out, not_360_out, F1, F0);
  and and_57 (BEQ, not_361_out, not_362_out, not_363_out, OP2, not_364_out, not_365_out);
  and and_58 (BNE, not_366_out, not_367_out, not_368_out, OP2, not_369_out, OP0);
  and and_59 (JR, not_370_out, not_371_out, not_372_out, not_373_out, not_374_out, not_375_out, not_376_out, not_377_out, F3, not_378_out, not_379_out, not_380_out);
  and and_60 (BGEZ, not_381_out, not_382_out, not_383_out, not_384_out, not_385_out, OP0);
  or or_1 (ALU_SRC, and_4_out, and_5_out, and_6_out, and_7_out, and_8_out, and_9_out, and_10_out, and_11_out, and_12_out);
  or or_2 (MemtoReg, and_35_out, and_36_out);
  or or_3 (SignedExt, and_37_out, and_38_out, and_39_out, and_40_out, and_41_out, and_42_out, and_43_out, and_44_out);
  or or_4 (RegWrite, and_13_out, and_14_out, and_15_out, and_16_out, and_17_out, and_18_out, and_19_out, and_20_out, and_21_out, and_22_out, and_23_out, and_24_out, and_25_out, and_26_out, and_27_out, and_28_out, and_29_out, and_30_out, and_31_out, and_32_out, and_33_out);
  or or_5 (RegDst, and_45_out, and_46_out, and_47_out, and_48_out, and_49_out, and_50_out, and_51_out, and_52_out, and_53_out, and_54_out, and_55_out, and_56_out);
endmodule

// ALU
module MIPS_ALU (
  input  [4:0] shamt,
  input  [31:0] X,
  input  [31:0] Y,
  input  [3:0] AluOP,
  output Equal,
  output [31:0] Result,
  output [31:0] Result_2
);

  wire [0:0] comparator_1_lt, comparator_2_lt;
  wire [31:0] adder_1_out, AND_out, divider_1_out, divider_1_rem, multiplier_1_cout, multiplier_1_out,
       NOR_out, OR_out, shifter_1_out, shifter_2_out, shifter_3_out, subtractor_1_out, XOR_out;

  assign AND_out = X & Y;  // AND_Gate AND, 32 bits wide
  assign OR_out = X | Y;  // OR_Gate OR, 32 bits wide
  Shifter #(.width(32)) shifter_1 (.in(Y), .\dist (shamt), .out(shifter_1_out));
  Shifter #(.width(32), .shift("ar")) shifter_2 (.in(Y), .\dist (shamt), .out(shifter_2_out));
  Shifter #(.width(32), .shift("lr")) shifter_3 (.in(Y), .\dist (shamt), .out(shifter_3_out));
  Multiplier #(.width(32)) multiplier_1 (.a(X), .b(Y), .out(multiplier_1_out), .cout(multiplier_1_cout));  // open: cin
  Divider #(.width(32)) divider_1 (.a(X), .b(Y), .out(divider_1_out), .rem(divider_1_rem));  // open: upper
  Adder #(.width(32)) adder_1 (.a(X), .b(Y), .out(adder_1_out));  // open: cin, cout
  Subtractor #(.width(32)) subtractor_1 (.a(X), .b(Y), .out(subtractor_1_out));  // open: bin, bout
  assign XOR_out = X ^ Y;  // XOR_Gate XOR, 32 bits wide
  assign NOR_out = ~(X | Y);  // NOR_Gate NOR, 32 bits wide
  Comparator #(.width(32)) comparator_1 (.a(X), .b(Y), .eq(Equal), .lt(comparator_1_lt[0]));  // open: gt
  Comparator #(.width(32), .mode("unsigned")) comparator_2 (.a(X), .b(Y), .lt(comparator_2_lt[0]));  // open: gt, eq
  Multiplexer #(.select(4), .width(32), .enable("false")) multiplexer_1 (
    .in0(shifter_1_out), .in1(shifter_2_out), .in2(shifter_3_out), .in3(multiplier_1_out),
    .in4(divider_1_out), .in5(adder_1_out), .in6(subtractor_1_out), .in7(AND_out), .in8(OR_out),
    .in9(XOR_out), .in10(NOR_out), .in11({{31{1'b0}}, comparator_1_lt[0]}),
    .in12({{31{1'b0}}, comparator_2_lt[0]}), .in13({32{1'b0}}), .in14({32{1'b0}}), .in15({32{1'b0}}),
    .out(Result), .sel(AluOP));
  Multiplexer #(.select(4), .width(32), .enable("false")) multiplexer_2 (
    .in0({32{1'b0}}), .in1({32{1'b0}}), .in2({32{1'b0}}), .in3(multiplier_1_cout), .in4(divider_1_rem),
    .in5({32{1'b0}}), .in6({32{1'b0}}), .in7({32{1'b0}}), .in8({32{1'b0}}), .in9({32{1'b0}}),
    .in10({32{1'b0}}), .in11({32{1'b0}}), .in12({32{1'b0}}), .in13({32{1'b0}}), .in14({32{1'b0}}),
    .in15({32{1'b0}}), .out(Result_2), .sel(AluOP));

  // Other names for the same wires on the sheet: Result2[31:0] = Result_2; S[3:0] = AluOP

  // Notes on the sheet:
  //   不要改变此引脚区域内容，也不要改变ALU封装形式
  //   输入引脚
  //   输出引脚
endmodule

module MIPS_Regifile (
  input  [31:0] Din,
  input  Clk,
  input  WE,
  input  [4:0] R1_num,
  input  [4:0] W_num,
  input  [4:0] R2_num,
  output [31:0] R1,
  output [31:0] R2
);

  // RegisterFile registerfile_1: pin names not known; wires that end beside it: Din, Clk, WE, W_num, R1_num, R2_num, R1, R2
endmodule

// IF/ID
module IF_ID (
  input  [31:0] PC,
  input  [31:0] PredictPC,
  input  [31:0] IR,
  input  Effective,
  input  Clear,
  input  Enable,
  input  clk,
  output [31:0] out_8,
  output [31:0] out_9,
  output [31:0] out_10,
  output out_11
);

  wire multiplexer_4_out, not_1_out;
  wire [31:0] multiplexer_1_out, multiplexer_2_out, multiplexer_3_out;

  Multiplexer #(.width(32), .enable("false")) multiplexer_1 (
    .in0(PC), .in1({32{1'b0}}), .out(multiplexer_1_out), .sel(Clear));
  Multiplexer #(.width(32), .enable("false")) multiplexer_2 (
    .in0(PredictPC), .in1({32{1'b0}}), .out(multiplexer_2_out), .sel(Clear));
  Multiplexer #(.width(32), .enable("false")) multiplexer_3 (
    .in0(IR), .in1({32{1'b0}}), .out(multiplexer_3_out), .sel(Clear));
  Multiplexer #(.enable("false")) multiplexer_4 (.in0(Effective), .in1(1'b0), .out(multiplexer_4_out), .sel(Clear));
  not not_1 (not_1_out, Enable);
  Register #(.width(32)) register_1 (.D(multiplexer_1_out), .en(not_1_out), .Q(out_8), .clk(clk));  // open: clr
  Register #(.width(32)) register_2 (.D(multiplexer_2_out), .en(not_1_out), .Q(out_9), .clk(clk));  // open: clr
  Register #(.width(32)) register_3 (.D(multiplexer_3_out), .en(not_1_out), .Q(out_10), .clk(clk));  // open: clr
  Register #(.width(1)) register_4 (.D(multiplexer_4_out), .en(not_1_out), .Q(out_11), .clk(clk));  // open: clr
endmodule

// ID/EX
module ID_EX (
  input  Syscall,
  input  JAL,
  input  RegWrite,
  input  MemToReg,
  input  MemWrite,
  input  JR,
  input  JMP,
  input  Beq,
  input  Bne,
  input  [3:0] AluOP,
  input  AluSrcB,
  input  MemAccess,
  input  BGEZ,
  input  [1:0] R1_Forward,
  input  [1:0] R2_Forward,
  input  [31:0] R1,
  input  [31:0] R2,
  input  [4:0] Rd,
  input  [31:0] Imm,
  input  [4:0] Shamt,
  input  [25:0] j_addr,
  input  [31:0] PC,
  input  [31:0] PredictPC,
  input  [31:0] IR,
  input  Effective,
  input  Clear,
  input  Enable,
  input  clk,
  output out_29,
  output out_30,
  output out_31,
  output out_32,
  output out_33,
  output out_34,
  output out_35,
  output out_36,
  output out_37,
  output [3:0] out_38,
  output out_39,
  output out_40,
  output out_41,
  output [1:0] out_42,
  output [1:0] out_43,
  output [31:0] out_44,
  output [31:0] out_45,
  output [4:0] out_46,
  output [31:0] out_47,
  output [4:0] out_48,
  output [25:0] out_49,
  output [31:0] out_50,
  output [31:0] out_51,
  output [31:0] out_52,
  output out_53
);

  wire multiplexer_2_out, multiplexer_3_out, multiplexer_15_out, not_1_out;
  wire [1:0] multiplexer_4_out, multiplexer_5_out;
  wire [4:0] multiplexer_8_out, multiplexer_10_out;
  wire [13:0] multiplexer_1_out;
  wire [25:0] multiplexer_11_out;
  wire [31:0] multiplexer_6_out, multiplexer_7_out, multiplexer_9_out, multiplexer_12_out,
       multiplexer_13_out, multiplexer_14_out;

  Multiplexer #(.width(14), .enable("false")) multiplexer_1 (
    .in0({AluSrcB, AluOP, Bne, Beq, JMP, JR, MemWrite, MemToReg, RegWrite, JAL, Syscall}), .in1({14{1'b0}}),
    .out(multiplexer_1_out), .sel(Clear));
  Multiplexer #(.enable("false")) multiplexer_2 (.in0(MemAccess), .in1(1'b0), .out(multiplexer_2_out), .sel(Clear));
  Multiplexer #(.enable("false")) multiplexer_3 (.in0(BGEZ), .in1(1'b0), .out(multiplexer_3_out), .sel(Clear));
  Multiplexer #(.width(2), .enable("false")) multiplexer_4 (
    .in0(R1_Forward), .in1(2'b00), .out(multiplexer_4_out), .sel(Clear));
  Multiplexer #(.width(2), .enable("false")) multiplexer_5 (
    .in0(R2_Forward), .in1(2'b00), .out(multiplexer_5_out), .sel(Clear));
  Multiplexer #(.width(32), .enable("false")) multiplexer_6 (
    .in0(R1), .in1({32{1'b0}}), .out(multiplexer_6_out), .sel(Clear));
  Multiplexer #(.width(32), .enable("false")) multiplexer_7 (
    .in0(R2), .in1({32{1'b0}}), .out(multiplexer_7_out), .sel(Clear));
  Multiplexer #(.width(5), .enable("false")) multiplexer_8 (
    .in0(Rd), .in1({5{1'b0}}), .out(multiplexer_8_out), .sel(Clear));
  Multiplexer #(.width(32), .enable("false")) multiplexer_9 (
    .in0(Imm), .in1({32{1'b0}}), .out(multiplexer_9_out), .sel(Clear));
  Multiplexer #(.width(5), .enable("false")) multiplexer_10 (
    .in0(Shamt), .in1({5{1'b0}}), .out(multiplexer_10_out), .sel(Clear));
  Multiplexer #(.width(26), .enable("false")) multiplexer_11 (
    .in0(j_addr), .in1({26{1'b0}}), .out(multiplexer_11_out), .sel(Clear));
  Multiplexer #(.width(32), .enable("false")) multiplexer_12 (
    .in0(PC), .in1({32{1'b0}}), .out(multiplexer_12_out), .sel(Clear));
  Multiplexer #(.width(32), .enable("false")) multiplexer_13 (
    .in0(PredictPC), .in1({32{1'b0}}), .out(multiplexer_13_out), .sel(Clear));
  Multiplexer #(.width(32), .enable("false")) multiplexer_14 (
    .in0(IR), .in1({32{1'b0}}), .out(multiplexer_14_out), .sel(Clear));
  Multiplexer #(.enable("false")) multiplexer_15 (.in0(Effective), .in1(1'b0), .out(multiplexer_15_out), .sel(Clear));
  not not_1 (not_1_out, Enable);
  Register #(.width(14)) register_1 (
    .D(multiplexer_1_out), .en(not_1_out),
    .Q({out_39, out_38, out_37, out_36, out_35, out_34, out_33, out_32, out_31, out_30, out_29}), .clk(clk));  // open: clr
  Register #(.width(1)) register_2 (.D(multiplexer_2_out), .en(not_1_out), .Q(out_40), .clk(clk));  // open: clr
  Register #(.width(1)) register_3 (.D(multiplexer_3_out), .en(not_1_out), .Q(out_41), .clk(clk));  // open: clr
  Register #(.width(2)) register_4 (.D(multiplexer_4_out), .en(not_1_out), .Q(out_42), .clk(clk));  // open: clr
  Register #(.width(2)) register_5 (.D(multiplexer_5_out), .en(not_1_out), .Q(out_43), .clk(clk));  // open: clr
  Register #(.width(32)) register_6 (.D(multiplexer_6_out), .en(not_1_out), .Q(out_44), .clk(clk));  // open: clr
  Register #(.width(32)) register_7 (.D(multiplexer_7_out), .en(not_1_out), .Q(out_45), .clk(clk));  // open: clr
  Register #(.width(5)) register_8 (.D(multiplexer_8_out), .en(not_1_out), .Q(out_46), .clk(clk));  // open: clr
  Register #(.width(32)) register_9 (.D(multiplexer_9_out), .en(not_1_out), .Q(out_47), .clk(clk));  // open: clr
  Register #(.width(5)) register_10 (.D(multiplexer_10_out), .en(not_1_out), .Q(out_48), .clk(clk));  // open: clr
  Register #(.width(26)) register_11 (.D(multiplexer_11_out), .en(not_1_out), .Q(out_49), .clk(clk));  // open: clr
  Register #(.width(32)) register_12 (.D(multiplexer_12_out), .en(not_1_out), .Q(out_50), .clk(clk));  // open: clr
  Register #(.width(32)) register_13 (.D(multiplexer_13_out), .en(not_1_out), .Q(out_51), .clk(clk));  // open: clr
  Register #(.width(32)) register_14 (.D(multiplexer_14_out), .en(not_1_out), .Q(out_52), .clk(clk));  // open: clr
  Register #(.width(1)) register_15 (.D(multiplexer_15_out), .en(not_1_out), .Q(out_53), .clk(clk));  // open: clr
endmodule

// EX/MEM
module EX_MEM (
  input  Syscall,
  input  JAL,
  input  RegWrite,
  input  MemToReg,
  input  MemWrite,
  input  MemAccess,
  input  [31:0] alu_result1,
  input  [31:0] R1,
  input  [31:0] R2,
  input  [4:0] Rd,
  input  [31:0] IR,
  input  [31:0] PC,
  input  Effective,
  input  Clear,
  input  Enable,
  input  clk,
  output out_17,
  output out_18,
  output out_19,
  output out_20,
  output out_21,
  output out_22,
  output [31:0] out_23,
  output [31:0] out_24,
  output [31:0] out_25,
  output [4:0] out_26,
  output [31:0] out_27,
  output [31:0] out_28,
  output out_29
);

  wire multiplexer_1_out, multiplexer_2_out, multiplexer_3_out, multiplexer_4_out, multiplexer_5_out,
       multiplexer_6_out, multiplexer_13_out, not_1_out;
  wire [4:0] multiplexer_10_out;
  wire [31:0] multiplexer_7_out, multiplexer_8_out, multiplexer_9_out, multiplexer_11_out, multiplexer_12_out;

  Multiplexer #(.enable("false")) multiplexer_1 (.in0(Syscall), .in1(1'b0), .out(multiplexer_1_out), .sel(Clear));
  Multiplexer #(.enable("false")) multiplexer_2 (.in0(JAL), .in1(1'b0), .out(multiplexer_2_out), .sel(Clear));
  Multiplexer #(.enable("false")) multiplexer_3 (.in0(RegWrite), .in1(1'b0), .out(multiplexer_3_out), .sel(Clear));
  Multiplexer #(.enable("false")) multiplexer_4 (.in0(MemToReg), .in1(1'b0), .out(multiplexer_4_out), .sel(Clear));
  Multiplexer #(.enable("false")) multiplexer_5 (.in0(MemWrite), .in1(1'b0), .out(multiplexer_5_out), .sel(Clear));
  Multiplexer #(.enable("false")) multiplexer_6 (.in0(MemAccess), .in1(1'b0), .out(multiplexer_6_out), .sel(Clear));
  Multiplexer #(.width(32), .enable("false")) multiplexer_7 (
    .in0(alu_result1), .in1({32{1'b0}}), .out(multiplexer_7_out), .sel(Clear));
  Multiplexer #(.width(32), .enable("false")) multiplexer_8 (
    .in0(R1), .in1({32{1'b0}}), .out(multiplexer_8_out), .sel(Clear));
  Multiplexer #(.width(32), .enable("false")) multiplexer_9 (
    .in0(R2), .in1({32{1'b0}}), .out(multiplexer_9_out), .sel(Clear));
  Multiplexer #(.width(5), .enable("false")) multiplexer_10 (
    .in0(Rd), .in1({5{1'b0}}), .out(multiplexer_10_out), .sel(Clear));
  Multiplexer #(.width(32), .enable("false")) multiplexer_11 (
    .in0(IR), .in1({32{1'b0}}), .out(multiplexer_11_out), .sel(Clear));
  Multiplexer #(.width(32), .enable("false")) multiplexer_12 (
    .in0(PC), .in1({32{1'b0}}), .out(multiplexer_12_out), .sel(Clear));
  Multiplexer #(.enable("false")) multiplexer_13 (.in0(Effective), .in1(1'b0), .out(multiplexer_13_out), .sel(Clear));
  not not_1 (not_1_out, Enable);
  Register #(.width(1)) register_1 (.D(multiplexer_1_out), .en(not_1_out), .Q(out_17), .clk(clk));  // open: clr
  Register #(.width(1)) register_2 (.D(multiplexer_2_out), .en(not_1_out), .Q(out_18), .clk(clk));  // open: clr
  Register #(.width(1)) register_3 (.D(multiplexer_3_out), .en(not_1_out), .Q(out_19), .clk(clk));  // open: clr
  Register #(.width(1)) register_4 (.D(multiplexer_4_out), .en(not_1_out), .Q(out_20), .clk(clk));  // open: clr
  Register #(.width(1)) register_5 (.D(multiplexer_5_out), .en(not_1_out), .Q(out_21), .clk(clk));  // open: clr
  Register #(.width(1)) register_6 (.D(multiplexer_6_out), .en(not_1_out), .Q(out_22), .clk(clk));  // open: clr
  Register #(.width(32)) register_7 (.D(multiplexer_7_out), .en(not_1_out), .Q(out_23), .clk(clk));  // open: clr
  Register #(.width(32)) register_8 (.D(multiplexer_8_out), .en(not_1_out), .Q(out_24), .clk(clk));  // open: clr
  Register #(.width(32)) register_9 (.D(multiplexer_9_out), .en(not_1_out), .Q(out_25), .clk(clk));  // open: clr
  Register #(.width(5)) register_10 (.D(multiplexer_10_out), .en(not_1_out), .Q(out_26), .clk(clk));  // open: clr
  Register #(.width(32)) register_11 (.D(multiplexer_11_out), .en(not_1_out), .Q(out_27), .clk(clk));  // open: clr
  Register #(.width(32)) register_12 (.D(multiplexer_12_out), .en(not_1_out), .Q(out_28), .clk(clk));  // open: clr
  Register #(.width(1)) register_13 (.D(multiplexer_13_out), .en(not_1_out), .Q(out_29), .clk(clk));  // open: clr
endmodule

// MEM/WB
module MEM_WB (
  input  Syscall,
  input  JAL,
  input  RegWrite,
  input  [31:0] R1,
  input  [31:0] R2,
  input  [4:0] Rd,
  input  [31:0] write_back,
  input  [31:0] IR,
  input  [31:0] PC,
  input  Effective,
  input  Clear,
  input  Enable,
  input  clk,
  output out_14,
  output out_15,
  output out_16,
  output [31:0] out_17,
  output [31:0] out_18,
  output [4:0] out_19,
  output [31:0] out_20,
  output [31:0] out_21,
  output [31:0] out_22,
  output out_23
);

  wire multiplexer_1_out, multiplexer_2_out, multiplexer_3_out, multiplexer_10_out, not_1_out;
  wire [4:0] multiplexer_6_out;
  wire [31:0] multiplexer_4_out, multiplexer_5_out, multiplexer_7_out, multiplexer_8_out, multiplexer_9_out;

  Multiplexer #(.enable("false")) multiplexer_1 (.in0(Syscall), .in1(1'b0), .out(multiplexer_1_out), .sel(Clear));
  Multiplexer #(.enable("false")) multiplexer_2 (.in0(JAL), .in1(1'b0), .out(multiplexer_2_out), .sel(Clear));
  Multiplexer #(.enable("false")) multiplexer_3 (.in0(RegWrite), .in1(1'b0), .out(multiplexer_3_out), .sel(Clear));
  Multiplexer #(.width(32), .enable("false")) multiplexer_4 (
    .in0(R1), .in1({32{1'b0}}), .out(multiplexer_4_out), .sel(Clear));
  Multiplexer #(.width(32), .enable("false")) multiplexer_5 (
    .in0(R2), .in1({32{1'b0}}), .out(multiplexer_5_out), .sel(Clear));
  Multiplexer #(.width(5), .enable("false")) multiplexer_6 (
    .in0(Rd), .in1({5{1'b0}}), .out(multiplexer_6_out), .sel(Clear));
  Multiplexer #(.width(32), .enable("false")) multiplexer_7 (
    .in0(write_back), .in1({32{1'b0}}), .out(multiplexer_7_out), .sel(Clear));
  Multiplexer #(.width(32), .enable("false")) multiplexer_8 (
    .in0(IR), .in1({32{1'b0}}), .out(multiplexer_8_out), .sel(Clear));
  Multiplexer #(.width(32), .enable("false")) multiplexer_9 (
    .in0(PC), .in1({32{1'b0}}), .out(multiplexer_9_out), .sel(Clear));
  Multiplexer #(.enable("false")) multiplexer_10 (.in0(Effective), .in1(1'b0), .out(multiplexer_10_out), .sel(Clear));
  not not_1 (not_1_out, Enable);
  Register #(.width(1)) register_1 (.D(multiplexer_1_out), .en(not_1_out), .Q(out_14), .clk(clk));  // open: clr
  Register #(.width(1)) register_2 (.D(multiplexer_2_out), .en(not_1_out), .Q(out_15), .clk(clk));  // open: clr
  Register #(.width(1)) register_3 (.D(multiplexer_3_out), .en(not_1_out), .Q(out_16), .clk(clk));  // open: clr
  Register #(.width(32)) register_4 (.D(multiplexer_4_out), .en(not_1_out), .Q(out_17), .clk(clk));  // open: clr
  Register #(.width(32)) register_5 (.D(multiplexer_5_out), .en(not_1_out), .Q(out_18), .clk(clk));  // open: clr
  Register #(.width(5)) register_6 (.D(multiplexer_6_out), .en(not_1_out), .Q(out_19), .clk(clk));  // open: clr
  Register #(.width(32)) register_7 (.D(multiplexer_7_out), .en(not_1_out), .Q(out_20), .clk(clk));  // open: clr
  Register #(.width(32)) register_8 (.D(multiplexer_8_out), .en(not_1_out), .Q(out_21), .clk(clk));  // open: clr
  Register #(.width(32)) register_9 (.D(multiplexer_9_out), .en(not_1_out), .Q(out_22), .clk(clk));  // open: clr
  Register #(.width(1)) register_10 (.D(multiplexer_10_out), .en(not_1_out), .Q(out_23), .clk(clk));  // open: clr
endmodule
// 源寄存器使用情况
module \源寄存器使用情况  (
  input  [5:0] OP,
  input  [5:0] Func,
  output R1_Used,
  output R2_Used
);

  wire and_1_out, and_2_out, and_3_out, and_4_out, and_5_out, and_6_out, and_7_out, and_8_out, and_9_out,
       and_10_out, and_11_out, and_12_out, and_13_out, and_14_out, and_15_out, and_16_out, and_17_out,
       and_18_out, and_19_out, and_20_out, and_21_out, and_22_out, and_23_out, and_24_out, and_25_out,
       and_26_out, and_27_out, and_28_out, and_29_out, and_30_out, and_31_out, and_32_out, and_33_out,
       and_34_out, and_35_out, and_36_out, and_37_out, and_38_out, and_39_out, and_40_out, not_1_out,
       not_2_out, not_3_out, not_4_out, not_5_out, not_6_out, not_7_out, not_8_out, not_9_out, not_10_out,
       not_11_out, not_12_out, not_13_out, not_14_out, not_15_out, not_16_out, not_17_out, not_18_out,
       not_19_out, not_20_out, not_21_out, not_22_out, not_23_out, not_24_out, not_25_out, not_26_out,
       not_27_out, not_28_out, not_29_out, not_30_out, not_31_out, not_32_out, not_33_out, not_34_out,
       not_35_out, not_36_out, not_37_out, not_38_out, not_39_out, not_40_out, not_41_out, not_42_out,
       not_43_out, not_44_out, not_45_out, not_46_out, not_47_out, not_48_out, not_49_out, not_50_out,
       not_51_out, not_52_out, not_53_out, not_54_out, not_55_out, not_56_out, not_57_out, not_58_out,
       not_59_out, not_60_out, not_61_out, not_62_out, not_63_out, not_64_out, not_65_out, not_66_out,
       not_67_out, not_68_out, not_69_out, not_70_out, not_71_out, not_72_out, not_73_out, not_74_out,
       not_75_out, not_76_out, not_77_out, not_78_out, not_79_out, not_80_out, not_81_out, not_82_out,
       not_83_out, not_84_out, not_85_out, not_86_out, not_87_out, not_88_out, not_89_out, not_90_out,
       not_91_out, not_92_out, not_93_out, not_94_out, not_95_out, not_96_out, not_97_out, not_98_out,
       not_99_out, not_100_out, not_101_out, not_102_out, not_103_out, not_104_out, not_105_out, not_106_out,
       not_107_out, not_108_out, not_109_out, not_110_out, not_111_out, not_112_out, not_113_out,
       not_114_out, not_115_out, not_116_out, not_117_out, not_118_out, not_119_out, not_120_out,
       not_121_out, not_122_out, not_123_out, not_124_out, not_125_out, not_126_out, not_127_out,
       not_128_out, not_129_out, not_130_out, not_131_out, not_132_out, not_133_out, not_134_out,
       not_135_out, not_136_out, not_137_out, not_138_out, not_139_out, not_140_out, not_141_out,
       not_142_out, not_143_out, not_144_out, not_145_out, not_146_out, not_147_out, not_148_out,
       not_149_out, not_150_out, not_151_out, not_152_out, not_153_out, not_154_out, not_155_out,
       not_156_out, not_157_out, not_158_out, not_159_out, not_160_out, not_161_out, not_162_out,
       not_163_out, not_164_out, not_165_out, not_166_out, not_167_out, not_168_out, not_169_out,
       not_170_out, not_171_out, not_172_out, not_173_out, not_174_out, not_175_out, not_176_out,
       not_177_out, not_178_out, not_179_out, not_180_out, not_181_out, not_182_out, not_183_out,
       not_184_out, not_185_out, not_186_out, not_187_out, not_188_out, not_189_out, not_190_out,
       not_191_out, not_192_out, not_193_out, not_194_out, not_195_out, not_196_out, not_197_out,
       not_198_out, not_199_out, not_200_out, not_201_out, not_202_out, not_203_out, not_204_out,
       not_205_out, not_206_out, not_207_out, not_208_out, not_209_out, not_210_out, not_211_out,
       not_212_out, not_213_out, not_214_out, not_215_out, not_216_out, not_217_out, not_218_out,
       not_219_out, not_220_out, not_221_out, not_222_out, not_223_out, not_224_out, not_225_out,
       not_226_out, not_227_out, not_228_out, not_229_out, not_230_out, not_231_out, not_232_out,
       not_233_out, not_234_out, not_235_out, not_236_out, not_237_out, not_238_out, not_239_out,
       not_240_out, not_241_out, not_242_out, not_243_out, not_244_out, not_245_out, not_246_out,
       not_247_out, not_248_out, not_249_out, not_250_out, not_251_out, not_252_out, not_253_out,
       not_254_out, not_255_out, not_256_out, not_257_out, not_258_out, not_259_out, not_260_out,
       not_261_out, not_262_out, not_263_out, not_264_out, not_265_out, not_266_out, not_267_out,
       not_268_out, not_269_out, not_270_out, not_271_out, not_272_out, not_273_out, not_274_out,
       not_275_out, not_276_out, not_277_out, not_278_out, not_279_out, not_280_out, not_281_out,
       not_282_out, not_283_out, not_284_out, not_285_out, not_286_out, not_287_out, not_288_out,
       not_289_out, not_290_out, not_291_out, not_292_out, not_293_out, not_294_out;

  not not_1 (not_1_out, OP[5]);
  not not_2 (not_2_out, OP[4]);
  not not_3 (not_3_out, OP[3]);
  not not_4 (not_4_out, OP[2]);
  not not_5 (not_5_out, OP[1]);
  not not_6 (not_6_out, OP[0]);
  not not_7 (not_7_out, Func[4]);
  not not_8 (not_8_out, Func[3]);
  not not_9 (not_9_out, Func[2]);
  not not_10 (not_10_out, Func[1]);
  not not_11 (not_11_out, Func[0]);
  not not_12 (not_12_out, OP[5]);
  not not_13 (not_13_out, OP[4]);
  not not_14 (not_14_out, OP[3]);
  not not_15 (not_15_out, OP[2]);
  not not_16 (not_16_out, OP[1]);
  not not_17 (not_17_out, OP[0]);
  not not_18 (not_18_out, Func[4]);
  not not_19 (not_19_out, Func[3]);
  not not_20 (not_20_out, Func[2]);
  not not_21 (not_21_out, Func[1]);
  not not_22 (not_22_out, OP[5]);
  not not_23 (not_23_out, OP[4]);
  not not_24 (not_24_out, OP[3]);
  not not_25 (not_25_out, OP[2]);
  not not_26 (not_26_out, OP[1]);
  not not_27 (not_27_out, OP[0]);
  not not_28 (not_28_out, Func[4]);
  not not_29 (not_29_out, Func[3]);
  not not_30 (not_30_out, Func[2]);
  not not_31 (not_31_out, Func[0]);
  not not_32 (not_32_out, OP[5]);
  not not_33 (not_33_out, OP[4]);
  not not_34 (not_34_out, OP[3]);
  not not_35 (not_35_out, OP[2]);
  not not_36 (not_36_out, OP[1]);
  not not_37 (not_37_out, OP[0]);
  not not_38 (not_38_out, Func[4]);
  not not_39 (not_39_out, Func[3]);
  not not_40 (not_40_out, Func[1]);
  not not_41 (not_41_out, Func[0]);
  not not_42 (not_42_out, OP[5]);
  not not_43 (not_43_out, OP[4]);
  not not_44 (not_44_out, OP[3]);
  not not_45 (not_45_out, OP[2]);
  not not_46 (not_46_out, OP[1]);
  not not_47 (not_47_out, OP[0]);
  not not_48 (not_48_out, Func[4]);
  not not_49 (not_49_out, Func[3]);
  not not_50 (not_50_out, Func[1]);
  not not_51 (not_51_out, OP[5]);
  not not_52 (not_52_out, OP[4]);
  not not_53 (not_53_out, OP[3]);
  not not_54 (not_54_out, OP[2]);
  not not_55 (not_55_out, OP[1]);
  not not_56 (not_56_out, OP[0]);
  not not_57 (not_57_out, Func[4]);
  not not_58 (not_58_out, Func[3]);
  not not_59 (not_59_out, OP[5]);
  not not_60 (not_60_out, OP[4]);
  not not_61 (not_61_out, OP[3]);
  not not_62 (not_62_out, OP[2]);
  not not_63 (not_63_out, OP[1]);
  not not_64 (not_64_out, OP[0]);
  not not_65 (not_65_out, Func[4]);
  not not_66 (not_66_out, Func[2]);
  not not_67 (not_67_out, Func[0]);
  not not_68 (not_68_out, OP[5]);
  not not_69 (not_69_out, OP[4]);
  not not_70 (not_70_out, OP[3]);
  not not_71 (not_71_out, OP[2]);
  not not_72 (not_72_out, OP[1]);
  not not_73 (not_73_out, OP[0]);
  not not_74 (not_74_out, Func[4]);
  not not_75 (not_75_out, Func[2]);
  not not_76 (not_76_out, OP[5]);
  not not_77 (not_77_out, OP[4]);
  not not_78 (not_78_out, OP[3]);
  not not_79 (not_79_out, OP[2]);
  not not_80 (not_80_out, OP[1]);
  not not_81 (not_81_out, OP[0]);
  not not_82 (not_82_out, Func[5]);
  not not_83 (not_83_out, Func[4]);
  not not_84 (not_84_out, Func[2]);
  not not_85 (not_85_out, Func[1]);
  not not_86 (not_86_out, Func[0]);
  not not_87 (not_87_out, OP[5]);
  not not_88 (not_88_out, OP[4]);
  not not_89 (not_89_out, OP[3]);
  not not_90 (not_90_out, OP[2]);
  not not_91 (not_91_out, OP[1]);
  not not_92 (not_92_out, OP[0]);
  not not_93 (not_93_out, Func[5]);
  not not_94 (not_94_out, Func[4]);
  not not_95 (not_95_out, Func[1]);
  not not_96 (not_96_out, Func[0]);
  not not_97 (not_97_out, OP[5]);
  not not_98 (not_98_out, OP[4]);
  not not_99 (not_99_out, OP[3]);
  not not_100 (not_100_out, OP[2]);
  not not_101 (not_101_out, OP[1]);
  not not_102 (not_102_out, OP[0]);
  not not_103 (not_103_out, Func[4]);
  not not_104 (not_104_out, Func[3]);
  not not_105 (not_105_out, Func[2]);
  not not_106 (not_106_out, OP[5]);
  not not_107 (not_107_out, OP[4]);
  not not_108 (not_108_out, OP[3]);
  not not_109 (not_109_out, OP[2]);
  not not_110 (not_110_out, OP[1]);
  not not_111 (not_111_out, OP[0]);
  not not_112 (not_112_out, Func[5]);
  not not_113 (not_113_out, Func[4]);
  not not_114 (not_114_out, Func[3]);
  not not_115 (not_115_out, Func[2]);
  not not_116 (not_116_out, Func[1]);
  not not_117 (not_117_out, Func[0]);
  not not_118 (not_118_out, OP[5]);
  not not_119 (not_119_out, OP[4]);
  not not_120 (not_120_out, OP[3]);
  not not_121 (not_121_out, OP[2]);
  not not_122 (not_122_out, OP[1]);
  not not_123 (not_123_out, OP[0]);
  not not_124 (not_124_out, Func[5]);
  not not_125 (not_125_out, Func[4]);
  not not_126 (not_126_out, Func[3]);
  not not_127 (not_127_out, Func[2]);
  not not_128 (not_128_out, OP[5]);
  not not_129 (not_129_out, OP[4]);
  not not_130 (not_130_out, OP[3]);
  not not_131 (not_131_out, OP[2]);
  not not_132 (not_132_out, OP[1]);
  not not_133 (not_133_out, OP[0]);
  not not_134 (not_134_out, Func[5]);
  not not_135 (not_135_out, Func[4]);
  not not_136 (not_136_out, Func[3]);
  not not_137 (not_137_out, Func[2]);
  not not_138 (not_138_out, Func[0]);
  not not_139 (not_139_out, OP[5]);
  not not_140 (not_140_out, OP[4]);
  not not_141 (not_141_out, OP[3]);
  not not_142 (not_142_out, OP[2]);
  not not_143 (not_143_out, OP[1]);
  not not_144 (not_144_out, OP[0]);
  not not_145 (not_145_out, Func[4]);
  not not_146 (not_146_out, Func[3]);
  not not_147 (not_147_out, Func[2]);
  not not_148 (not_148_out, Func[1]);
  not not_149 (not_149_out, Func[0]);
  not not_150 (not_150_out, OP[5]);
  not not_151 (not_151_out, OP[4]);
  not not_152 (not_152_out, OP[3]);
  not not_153 (not_153_out, OP[2]);
  not not_154 (not_154_out, OP[1]);
  not not_155 (not_155_out, OP[0]);
  not not_156 (not_156_out, Func[4]);
  not not_157 (not_157_out, Func[3]);
  not not_158 (not_158_out, Func[2]);
  not not_159 (not_159_out, Func[1]);
  not not_160 (not_160_out, OP[5]);
  not not_161 (not_161_out, OP[4]);
  not not_162 (not_162_out, OP[3]);
  not not_163 (not_163_out, OP[2]);
  not not_164 (not_164_out, OP[1]);
  not not_165 (not_165_out, OP[0]);
  not not_166 (not_166_out, Func[4]);
  not not_167 (not_167_out, Func[3]);
  not not_168 (not_168_out, Func[2]);
  not not_169 (not_169_out, Func[0]);
  not not_170 (not_170_out, OP[5]);
  not not_171 (not_171_out, OP[4]);
  not not_172 (not_172_out, OP[3]);
  not not_173 (not_173_out, OP[2]);
  not not_174 (not_174_out, OP[1]);
  not not_175 (not_175_out, OP[0]);
  not not_176 (not_176_out, Func[4]);
  not not_177 (not_177_out, Func[3]);
  not not_178 (not_178_out, Func[1]);
  not not_179 (not_179_out, Func[0]);
  not not_180 (not_180_out, OP[5]);
  not not_181 (not_181_out, OP[4]);
  not not_182 (not_182_out, OP[3]);
  not not_183 (not_183_out, OP[2]);
  not not_184 (not_184_out, OP[1]);
  not not_185 (not_185_out, OP[0]);
  not not_186 (not_186_out, Func[4]);
  not not_187 (not_187_out, Func[3]);
  not not_188 (not_188_out, Func[1]);
  not not_189 (not_189_out, OP[5]);
  not not_190 (not_190_out, OP[4]);
  not not_191 (not_191_out, OP[3]);
  not not_192 (not_192_out, OP[2]);
  not not_193 (not_193_out, OP[1]);
  not not_194 (not_194_out, OP[0]);
  not not_195 (not_195_out, Func[4]);
  not not_196 (not_196_out, Func[3]);
  not not_197 (not_197_out, OP[5]);
  not not_198 (not_198_out, OP[4]);
  not not_199 (not_199_out, OP[3]);
  not not_200 (not_200_out, OP[2]);
  not not_201 (not_201_out, OP[1]);
  not not_202 (not_202_out, OP[0]);
  not not_203 (not_203_out, Func[4]);
  not not_204 (not_204_out, Func[2]);
  not not_205 (not_205_out, Func[0]);
  not not_206 (not_206_out, OP[5]);
  not not_207 (not_207_out, OP[4]);
  not not_208 (not_208_out, OP[3]);
  not not_209 (not_209_out, OP[2]);
  not not_210 (not_210_out, OP[1]);
  not not_211 (not_211_out, OP[0]);
  not not_212 (not_212_out, Func[4]);
  not not_213 (not_213_out, Func[2]);
  not not_214 (not_214_out, OP[5]);
  not not_215 (not_215_out, OP[4]);
  not not_216 (not_216_out, OP[3]);
  not not_217 (not_217_out, OP[2]);
  not not_218 (not_218_out, OP[1]);
  not not_219 (not_219_out, OP[0]);
  not not_220 (not_220_out, Func[5]);
  not not_221 (not_221_out, Func[4]);
  not not_222 (not_222_out, Func[1]);
  not not_223 (not_223_out, Func[0]);
  not not_224 (not_224_out, OP[5]);
  not not_225 (not_225_out, OP[4]);
  not not_226 (not_226_out, OP[3]);
  not not_227 (not_227_out, OP[2]);
  not not_228 (not_228_out, OP[1]);
  not not_229 (not_229_out, OP[0]);
  not not_230 (not_230_out, Func[4]);
  not not_231 (not_231_out, Func[3]);
  not not_232 (not_232_out, Func[2]);
  not not_233 (not_233_out, OP[5]);
  not not_234 (not_234_out, OP[4]);
  not not_235 (not_235_out, OP[3]);
  not not_236 (not_236_out, OP[1]);
  not not_237 (not_237_out, OP[0]);
  not not_238 (not_238_out, OP[5]);
  not not_239 (not_239_out, OP[4]);
  not not_240 (not_240_out, OP[3]);
  not not_241 (not_241_out, OP[1]);
  not not_242 (not_242_out, OP[5]);
  not not_243 (not_243_out, OP[4]);
  not not_244 (not_244_out, OP[2]);
  not not_245 (not_245_out, OP[1]);
  not not_246 (not_246_out, OP[0]);
  not not_247 (not_247_out, OP[5]);
  not not_248 (not_248_out, OP[4]);
  not not_249 (not_249_out, OP[1]);
  not not_250 (not_250_out, OP[0]);
  not not_251 (not_251_out, OP[5]);
  not not_252 (not_252_out, OP[4]);
  not not_253 (not_253_out, OP[2]);
  not not_254 (not_254_out, OP[1]);
  not not_255 (not_255_out, OP[5]);
  not not_256 (not_256_out, OP[4]);
  not not_257 (not_257_out, OP[2]);
  not not_258 (not_258_out, OP[0]);
  not not_259 (not_259_out, OP[5]);
  not not_260 (not_260_out, OP[4]);
  not not_261 (not_261_out, OP[1]);
  not not_262 (not_262_out, OP[4]);
  not not_263 (not_263_out, OP[3]);
  not not_264 (not_264_out, OP[2]);
  not not_265 (not_265_out, OP[4]);
  not not_266 (not_266_out, OP[2]);
  not not_267 (not_267_out, OP[5]);
  not not_268 (not_268_out, OP[4]);
  not not_269 (not_269_out, OP[0]);
  not not_270 (not_270_out, OP[4]);
  not not_271 (not_271_out, OP[3]);
  not not_272 (not_272_out, OP[2]);
  not not_273 (not_273_out, OP[1]);
  not not_274 (not_274_out, OP[5]);
  not not_275 (not_275_out, OP[4]);
  not not_276 (not_276_out, OP[3]);
  not not_277 (not_277_out, OP[2]);
  not not_278 (not_278_out, OP[1]);
  not not_279 (not_279_out, OP[5]);
  not not_280 (not_280_out, OP[4]);
  not not_281 (not_281_out, OP[3]);
  not not_282 (not_282_out, OP[1]);
  not not_283 (not_283_out, OP[0]);
  not not_284 (not_284_out, OP[5]);
  not not_285 (not_285_out, OP[4]);
  not not_286 (not_286_out, OP[3]);
  not not_287 (not_287_out, OP[1]);
  not not_288 (not_288_out, OP[4]);
  not not_289 (not_289_out, OP[2]);
  not not_290 (not_290_out, OP[5]);
  not not_291 (not_291_out, OP[4]);
  not not_292 (not_292_out, OP[3]);
  not not_293 (not_293_out, OP[2]);
  not not_294 (not_294_out, OP[1]);
  and and_1 (and_1_out, not_1_out, not_2_out, not_3_out, not_4_out, not_5_out, not_6_out, Func[5], not_7_out, not_8_out, not_9_out, not_10_out, not_11_out);
  and and_2 (and_2_out, not_12_out, not_13_out, not_14_out, not_15_out, not_16_out, not_17_out, Func[5], not_18_out, not_19_out, not_20_out, not_21_out, Func[0]);
  and and_3 (and_3_out, not_22_out, not_23_out, not_24_out, not_25_out, not_26_out, not_27_out, Func[5], not_28_out, not_29_out, not_30_out, Func[1], not_31_out);
  and and_4 (and_4_out, not_32_out, not_33_out, not_34_out, not_35_out, not_36_out, not_37_out, Func[5], not_38_out, not_39_out, Func[2], not_40_out, not_41_out);
  and and_5 (and_5_out, not_42_out, not_43_out, not_44_out, not_45_out, not_46_out, not_47_out, Func[5], not_48_out, not_49_out, Func[2], not_50_out, Func[0]);
  and and_6 (and_6_out, not_51_out, not_52_out, not_53_out, not_54_out, not_55_out, not_56_out, Func[5], not_57_out, not_58_out, Func[2], Func[1], Func[0]);
  and and_7 (and_7_out, not_59_out, not_60_out, not_61_out, not_62_out, not_63_out, not_64_out, Func[5], not_65_out, Func[3], not_66_out, Func[1], not_67_out);
  and and_8 (and_8_out, not_68_out, not_69_out, not_70_out, not_71_out, not_72_out, not_73_out, Func[5], not_74_out, Func[3], not_75_out, Func[1], Func[0]);
  and and_9 (and_9_out, not_76_out, not_77_out, not_78_out, not_79_out, not_80_out, not_81_out, not_82_out, not_83_out, Func[3], not_84_out, not_85_out, not_86_out);
  and and_10 (and_10_out, not_87_out, not_88_out, not_89_out, not_90_out, not_91_out, not_92_out, not_93_out, not_94_out, Func[3], Func[2], not_95_out, not_96_out);
  and and_11 (and_11_out, not_233_out, not_234_out, not_235_out, OP[2], not_236_out, not_237_out);
  and and_12 (and_12_out, not_238_out, not_239_out, not_240_out, OP[2], not_241_out, OP[0]);
  and and_13 (and_13_out, not_242_out, not_243_out, OP[3], not_244_out, not_245_out, not_246_out);
  and and_14 (and_14_out, not_247_out, not_248_out, OP[3], OP[2], not_249_out, not_250_out);
  and and_15 (and_15_out, not_251_out, not_252_out, OP[3], not_253_out, not_254_out, OP[0]);
  and and_16 (and_16_out, not_255_out, not_256_out, OP[3], not_257_out, OP[1], not_258_out);
  and and_17 (and_17_out, not_259_out, not_260_out, OP[3], OP[2], not_261_out, OP[0]);
  and and_18 (and_18_out, OP[5], not_262_out, not_263_out, not_264_out, OP[1], OP[0]);
  and and_19 (and_19_out, OP[5], not_265_out, OP[3], not_266_out, OP[1], OP[0]);
  and and_20 (and_20_out, not_97_out, not_98_out, not_99_out, not_100_out, not_101_out, not_102_out, Func[5], not_103_out, not_104_out, not_105_out, Func[1], Func[0]);
  and and_21 (and_21_out, not_267_out, not_268_out, OP[3], OP[2], OP[1], not_269_out);
  and and_22 (and_22_out, OP[5], not_270_out, not_271_out, not_272_out, not_273_out, OP[0]);
  and and_23 (and_23_out, not_274_out, not_275_out, not_276_out, not_277_out, not_278_out, OP[0]);
  and and_24 (and_24_out, not_106_out, not_107_out, not_108_out, not_109_out, not_110_out, not_111_out, not_112_out, not_113_out, not_114_out, not_115_out, not_116_out, not_117_out);
  and and_25 (and_25_out, not_118_out, not_119_out, not_120_out, not_121_out, not_122_out, not_123_out, not_124_out, not_125_out, not_126_out, not_127_out, Func[1], Func[0]);
  and and_26 (and_26_out, not_128_out, not_129_out, not_130_out, not_131_out, not_132_out, not_133_out, not_134_out, not_135_out, not_136_out, not_137_out, Func[1], not_138_out);
  and and_27 (and_27_out, not_139_out, not_140_out, not_141_out, not_142_out, not_143_out, not_144_out, Func[5], not_145_out, not_146_out, not_147_out, not_148_out, not_149_out);
  and and_28 (and_28_out, not_150_out, not_151_out, not_152_out, not_153_out, not_154_out, not_155_out, Func[5], not_156_out, not_157_out, not_158_out, not_159_out, Func[0]);
  and and_29 (and_29_out, not_160_out, not_161_out, not_162_out, not_163_out, not_164_out, not_165_out, Func[5], not_166_out, not_167_out, not_168_out, Func[1], not_169_out);
  and and_30 (and_30_out, not_170_out, not_171_out, not_172_out, not_173_out, not_174_out, not_175_out, Func[5], not_176_out, not_177_out, Func[2], not_178_out, not_179_out);
  and and_31 (and_31_out, not_180_out, not_181_out, not_182_out, not_183_out, not_184_out, not_185_out, Func[5], not_186_out, not_187_out, Func[2], not_188_out, Func[0]);
  and and_32 (and_32_out, not_189_out, not_190_out, not_191_out, not_192_out, not_193_out, not_194_out, Func[5], not_195_out, not_196_out, Func[2], Func[1], Func[0]);
  and and_33 (and_33_out, not_197_out, not_198_out, not_199_out, not_200_out, not_201_out, not_202_out, Func[5], not_203_out, Func[3], not_204_out, Func[1], not_205_out);
  and and_34 (and_34_out, not_206_out, not_207_out, not_208_out, not_209_out, not_210_out, not_211_out, Func[5], not_212_out, Func[3], not_213_out, Func[1], Func[0]);
  and and_35 (and_35_out, not_214_out, not_215_out, not_216_out, not_217_out, not_218_out, not_219_out, not_220_out, not_221_out, Func[3], Func[2], not_222_out, not_223_out);
  and and_36 (and_36_out, not_279_out, not_280_out, not_281_out, OP[2], not_282_out, not_283_out);
  and and_37 (and_37_out, not_284_out, not_285_out, not_286_out, OP[2], not_287_out, OP[0]);
  and and_38 (and_38_out, OP[5], not_288_out, OP[3], not_289_out, OP[1], OP[0]);
  and and_39 (and_39_out, not_224_out, not_225_out, not_226_out, not_227_out, not_228_out, not_229_out, Func[5], not_230_out, not_231_out, not_232_out, Func[1], Func[0]);
  and and_40 (and_40_out, not_290_out, not_291_out, not_292_out, not_293_out, not_294_out, OP[0]);
  or or_1 (R1_Used, and_1_out, and_2_out, and_3_out, and_4_out, and_5_out, and_6_out, and_7_out, and_8_out, and_9_out, and_10_out, and_11_out, and_12_out, and_13_out, and_14_out, and_15_out, and_16_out, and_17_out, and_18_out, and_19_out, and_20_out, and_21_out, and_22_out, and_23_out);
  or or_2 (R2_Used, and_24_out, and_25_out, and_26_out, and_27_out, and_28_out, and_29_out, and_30_out, and_31_out, and_32_out, and_33_out, and_34_out, and_35_out, and_36_out, and_37_out, and_38_out, and_39_out, and_40_out);
endmodule

// 数据相关检测
module \数据相关检测  (
  input  R1_Used,
  input  R2_Used,
  input  EX_RegWrite,
  input  MEM_RegWrite,
  input  [4:0] R1_num,
  input  [4:0] R2_num,
  input  [4:0] EX_WriteReg_num,
  input  [4:0] MEM_WriteReg_num,
  output R1_EX_Related,
  output R2_EX_Related,
  output R1_MEM_Related,
  output R2_MEM_Related
);

  wire and_1_out, and_2_out, and_3_out, and_4_out, comparator_1_eq, comparator_2_eq, comparator_3_eq,
       comparator_4_eq, comparator_5_eq, comparator_6_eq;

  Comparator #(.width(5)) comparator_1 (.a(R1_num), .b({5{1'b0}}), .eq(comparator_1_eq));  // open: gt, lt
  Comparator #(.width(5)) comparator_2 (.a({5{1'b0}}), .b(R2_num), .eq(comparator_2_eq));  // open: gt, lt
  Comparator #(.width(5)) comparator_3 (.a(R1_num), .b(EX_WriteReg_num), .eq(comparator_3_eq));  // open: gt, lt
  Comparator #(.width(5)) comparator_4 (.a(R2_num), .b(EX_WriteReg_num), .eq(comparator_4_eq));  // open: gt, lt
  Comparator #(.width(5)) comparator_5 (.a(R1_num), .b(MEM_WriteReg_num), .eq(comparator_5_eq));  // open: gt, lt
  Comparator #(.width(5)) comparator_6 (.a(R2_num), .b(MEM_WriteReg_num), .eq(comparator_6_eq));  // open: gt, lt
  and and_1 (and_1_out, EX_RegWrite, comparator_3_eq);
  and and_2 (and_2_out, EX_RegWrite, comparator_4_eq);
  and and_3 (and_3_out, MEM_RegWrite, comparator_5_eq);
  and and_4 (and_4_out, MEM_RegWrite, comparator_6_eq);
  and and_5 (R1_EX_Related, R1_Used, ~comparator_1_eq, and_1_out);  // AND_Gate
  and and_6 (R2_EX_Related, R2_Used, ~comparator_2_eq, and_2_out);  // AND_Gate
  and and_7 (R1_MEM_Related, R1_Used, ~comparator_1_eq, and_3_out);  // AND_Gate
  and and_8 (R2_MEM_Related, R2_Used, ~comparator_2_eq, and_4_out);  // AND_Gate
endmodule

// BHT
module BHT (
  input  [31:0] IF_PC,
  input  [31:0] EX_PC,
  input  [31:0] BranchPC,
  input  Success,
  input  hasBranch,
  input  clk,
  output [31:0] PredictAddr
);

  wire and_1_out, and_2_out, and_3_out, and_4_out, and_5_out, and_6_out, and_7_out, and_8_out, and_17_out,
       and_18_out, and_19_out, and_20_out, and_29_out, and_30_out, comparator_1_eq, comparator_2_eq,
       comparator_3_eq, comparator_4_eq, comparator_5_eq, comparator_6_eq, comparator_7_eq, comparator_8_eq,
       comparator_9_eq, comparator_10_eq, comparator_11_eq, comparator_12_eq, comparator_13_eq,
       comparator_14_eq, comparator_15_eq, comparator_16_eq, Hit, L0, L1, L2, L3, L4, L5, L6, L7, Miss,
       not_1_out, not_2_out, not_3_out, not_4_out, not_5_out, or_1_out, or_2_out, or_3_out, or_4_out,
       or_5_out, or_6_out, priority_encoder_1_en_out, Refresh, Replace, Replace0, Replace1, Replace2,
       Replace3, Replace4, Replace5, Replace6, Replace7, Reset0, Reset1, Reset2, Reset3, Reset4, Reset5,
       Reset6, Reset7, S0, S1, S2, S3, S4, S5, S6, S7, V0, V1, V2, V3, V4, V5, V6, V7;
  wire [1:0] NextState, or_10_out, PredictSel, register_17_q, register_18_q, register_19_q, register_20_q,
       register_21_q, register_22_q, register_23_q, register_24_q, State;
  wire [2:0] adder_2_out, EmptyPos, LongestNo, max3_1_max_num, max3_2_max_num, max3_3_max_num,
       max3_4_max_num, max3_5_max_num, max3_6_max_num, multiplexer_5_out, priority_encoder_1_out;
  wire [15:0] C0, C1, C2, C3, C4, C5, C6, C7, max3_1_max, max3_2_max, max3_3_max, max3_4_max, max3_5_max,
       max3_6_max;
  wire [31:0] adder_1_out, BranchAddr, multiplexer_1_out, register_25_q, register_26_q, register_27_q,
       register_28_q, register_29_q, register_30_q, register_31_q, register_32_q, Tag0, Tag1, Tag2, Tag3,
       Tag4, Tag5, Tag6, Tag7;

  and and_1 (and_1_out, Reset0, S0);
  and and_2 (and_2_out, Reset1, S1);
  and and_3 (and_3_out, Reset2, S2);
  and and_4 (and_4_out, Reset3, S3);
  and and_5 (and_5_out, Reset4, S4);
  and and_6 (and_6_out, Reset5, S5);
  and and_7 (and_7_out, Reset6, S6);
  and and_8 (and_8_out, Reset7, S7);
  or or_1 (or_1_out, and_1_out, L0);
  or or_2 (or_2_out, and_2_out, L1);
  or or_3 (or_3_out, and_3_out, L2);
  or or_4 (or_4_out, and_4_out, L3);
  or or_5 (or_5_out, and_5_out, L4);
  or or_6 (or_6_out, and_6_out, L5);
  // OR_Gate or_7 has open pins: in0=and_7_out, in1=L6, out=open
  // OR_Gate or_8 has open pins: in0=and_8_out, in1=L7, out=open
  Register #(.width(1)) register_1 (.D(1'b1), .en(S0), .Q(V0), .clk(clk));  // open: clr
  Register #(.width(1)) register_2 (.D(1'b1), .en(S1), .Q(V1), .clk(clk));  // open: clr
  Register #(.width(1)) register_3 (.D(1'b1), .en(S2), .Q(V2), .clk(clk));  // open: clr
  Register #(.width(1)) register_4 (.D(1'b1), .en(S3), .Q(V3), .clk(clk));  // open: clr
  Register #(.width(1)) register_5 (.D(1'b1), .en(S4), .Q(V4), .clk(clk));  // open: clr
  Register #(.width(1)) register_6 (.D(1'b1), .en(S5), .Q(V5), .clk(clk));  // open: clr
  Register #(.width(1)) register_7 (.D(1'b1), .en(S6), .Q(V6), .clk(clk));  // open: clr
  Register #(.width(1)) register_8 (.D(1'b1), .en(S7), .Q(V7), .clk(clk));  // open: clr
  Register #(.width(32)) register_9 (.D(EX_PC), .en(S0), .Q(Tag0), .clk(clk));  // open: clr
  Register #(.width(32)) register_10 (.D(EX_PC), .en(S1), .Q(Tag1), .clk(clk));  // open: clr
  Register #(.width(32)) register_11 (.D(EX_PC), .en(S2), .Q(Tag2), .clk(clk));  // open: clr
  Register #(.width(32)) register_12 (.D(EX_PC), .en(S3), .Q(Tag3), .clk(clk));  // open: clr
  Register #(.width(32)) register_13 (.D(EX_PC), .en(S4), .Q(Tag4), .clk(clk));  // open: clr
  Register #(.width(32)) register_14 (.D(EX_PC), .en(S5), .Q(Tag5), .clk(clk));  // open: clr
  Register #(.width(32)) register_15 (.D(EX_PC), .en(S6), .Q(Tag6), .clk(clk));  // open: clr
  Register #(.width(32)) register_16 (.D(EX_PC), .en(S7), .Q(Tag7), .clk(clk));  // open: clr
  syn_counter syn_counter_1 (.add1(Refresh), .clk(clk), .clr(S0), .Counter_out(C0));
  syn_counter syn_counter_2 (.add1(Refresh), .clk(clk), .clr(S1), .Counter_out(C1));
  syn_counter syn_counter_3 (.add1(Refresh), .clk(clk), .clr(S2), .Counter_out(C2));
  syn_counter syn_counter_4 (.add1(Refresh), .clk(clk), .clr(S3), .Counter_out(C3));
  syn_counter syn_counter_5 (.add1(Refresh), .clk(clk), .clr(S4), .Counter_out(C4));
  syn_counter syn_counter_6 (.add1(Refresh), .clk(clk), .clr(S5), .Counter_out(C5));
  syn_counter syn_counter_7 (.add1(Refresh), .clk(clk), .clr(S6), .Counter_out(C6));
  syn_counter syn_counter_8 (.add1(Refresh), .clk(clk), .clr(S7), .Counter_out(C7));
  Register #(.width(2)) register_17 (.D(NextState), .en(S0), .Q(register_17_q), .clk(clk));  // open: clr
  Register #(.width(2)) register_18 (.D(NextState), .en(S1), .Q(register_18_q), .clk(clk));  // open: clr
  Register #(.width(2)) register_19 (.D(NextState), .en(S2), .Q(register_19_q), .clk(clk));  // open: clr
  Register #(.width(2)) register_20 (.D(NextState), .en(S3), .Q(register_20_q), .clk(clk));  // open: clr
  Register #(.width(2)) register_21 (.D(NextState), .en(S4), .Q(register_21_q), .clk(clk));  // open: clr
  Register #(.width(2)) register_22 (.D(NextState), .en(S5), .Q(register_22_q), .clk(clk));  // open: clr
  Register #(.width(2)) register_23 (.D(NextState), .en(S6), .Q(register_23_q), .clk(clk));  // open: clr
  Register #(.width(2)) register_24 (.D(NextState), .en(S7), .Q(register_24_q), .clk(clk));  // open: clr
  assign State = S0 ? register_17_q : 2'bz;  // Controlled_Buffer controlled_buffer_1
  assign State = S1 ? register_18_q : 2'bz;  // Controlled_Buffer controlled_buffer_2
  assign State = S2 ? register_19_q : 2'bz;  // Controlled_Buffer controlled_buffer_3
  assign State = S3 ? register_20_q : 2'bz;  // Controlled_Buffer controlled_buffer_4
  assign State = S4 ? register_21_q : 2'bz;  // Controlled_Buffer controlled_buffer_5
  assign State = S5 ? register_22_q : 2'bz;  // Controlled_Buffer controlled_buffer_6
  assign State = S6 ? register_23_q : 2'bz;  // Controlled_Buffer controlled_buffer_7
  assign State = S7 ? register_24_q : 2'bz;  // Controlled_Buffer controlled_buffer_8
  assign PredictSel = L0 ? register_17_q : 2'bz;  // Controlled_Buffer controlled_buffer_9
  assign PredictSel = L1 ? register_18_q : 2'bz;  // Controlled_Buffer controlled_buffer_10
  assign PredictSel = L2 ? register_19_q : 2'bz;  // Controlled_Buffer controlled_buffer_11
  assign PredictSel = L3 ? register_20_q : 2'bz;  // Controlled_Buffer controlled_buffer_12
  assign PredictSel = L4 ? register_21_q : 2'bz;  // Controlled_Buffer controlled_buffer_13
  assign PredictSel = L5 ? register_22_q : 2'bz;  // Controlled_Buffer controlled_buffer_14
  assign PredictSel = L6 ? register_23_q : 2'bz;  // Controlled_Buffer controlled_buffer_15
  assign PredictSel = L7 ? register_24_q : 2'bz;  // Controlled_Buffer controlled_buffer_16
  Register #(.width(32)) register_25 (.D(BranchPC), .en(S0), .Q(register_25_q), .clk(clk));  // open: clr
  Register #(.width(32)) register_26 (.D(BranchPC), .en(S1), .Q(register_26_q), .clk(clk));  // open: clr
  Register #(.width(32)) register_27 (.D(BranchPC), .en(S2), .Q(register_27_q), .clk(clk));  // open: clr
  Register #(.width(32)) register_28 (.D(BranchPC), .en(S3), .Q(register_28_q), .clk(clk));  // open: clr
  Register #(.width(32)) register_29 (.D(BranchPC), .en(S4), .Q(register_29_q), .clk(clk));  // open: clr
  Register #(.width(32)) register_30 (.D(BranchPC), .en(S5), .Q(register_30_q), .clk(clk));  // open: clr
  Register #(.width(32)) register_31 (.D(BranchPC), .en(S6), .Q(register_31_q), .clk(clk));  // open: clr
  Register #(.width(32)) register_32 (.D(BranchPC), .en(S7), .Q(register_32_q), .clk(clk));  // open: clr
  assign BranchAddr = L0 ? register_25_q : 32'bz;  // Controlled_Buffer controlled_buffer_17
  assign BranchAddr = L1 ? register_26_q : 32'bz;  // Controlled_Buffer controlled_buffer_18
  assign BranchAddr = L2 ? register_27_q : 32'bz;  // Controlled_Buffer controlled_buffer_19
  assign BranchAddr = L3 ? register_28_q : 32'bz;  // Controlled_Buffer controlled_buffer_20
  assign BranchAddr = L4 ? register_29_q : 32'bz;  // Controlled_Buffer controlled_buffer_21
  assign BranchAddr = L5 ? register_30_q : 32'bz;  // Controlled_Buffer controlled_buffer_22
  assign BranchAddr = L6 ? register_31_q : 32'bz;  // Controlled_Buffer controlled_buffer_23
  assign BranchAddr = L7 ? register_32_q : 32'bz;  // Controlled_Buffer controlled_buffer_24
  Comparator #(.width(32)) comparator_1 (.a(IF_PC), .b(Tag0), .eq(comparator_1_eq));  // open: gt, lt
  Comparator #(.width(32)) comparator_2 (.a(IF_PC), .b(Tag1), .eq(comparator_2_eq));  // open: gt, lt
  Comparator #(.width(32)) comparator_3 (.a(IF_PC), .b(Tag2), .eq(comparator_3_eq));  // open: gt, lt
  Comparator #(.width(32)) comparator_4 (.a(IF_PC), .b(Tag3), .eq(comparator_4_eq));  // open: gt, lt
  Comparator #(.width(32)) comparator_5 (.a(IF_PC), .b(Tag4), .eq(comparator_5_eq));  // open: gt, lt
  Comparator #(.width(32)) comparator_6 (.a(IF_PC), .b(Tag5), .eq(comparator_6_eq));  // open: gt, lt
  Comparator #(.width(32)) comparator_7 (.a(IF_PC), .b(Tag6), .eq(comparator_7_eq));  // open: gt, lt
  Comparator #(.width(32)) comparator_8 (.a(IF_PC), .b(Tag7), .eq(comparator_8_eq));  // open: gt, lt
  and and_9 (L0, comparator_1_eq, V0);
  and and_10 (L1, comparator_2_eq, V1);
  and and_11 (L2, comparator_3_eq, V2);
  and and_12 (L3, comparator_4_eq, V3);
  and and_13 (L4, comparator_5_eq, V4);
  and and_14 (L5, comparator_6_eq, V5);
  and and_15 (L6, comparator_7_eq, V6);
  and and_16 (L7, comparator_8_eq, V7);
  not not_1 (not_1_out, State[0]);
  not not_2 (not_2_out, Success);
  not not_3 (not_3_out, State[0]);
  not not_4 (not_4_out, State[1]);
  not not_5 (not_5_out, State[0]);
  and and_17 (and_17_out, State[1], not_1_out);
  and and_18 (and_18_out, Success, State[0]);
  and and_19 (and_19_out, not_2_out, State[1], not_3_out);
  and and_20 (and_20_out, Success, not_4_out, not_5_out);
  Adder #(.width(32)) adder_1 (.a(IF_PC), .b(32'h4), .out(adder_1_out));  // open: cin, cout
  Comparator #(.width(32)) comparator_9 (.a(EX_PC), .b(Tag0), .eq(comparator_9_eq));  // open: gt, lt
  Comparator #(.width(32)) comparator_10 (.a(EX_PC), .b(Tag1), .eq(comparator_10_eq));  // open: gt, lt
  Comparator #(.width(32)) comparator_11 (.a(EX_PC), .b(Tag2), .eq(comparator_11_eq));  // open: gt, lt
  Comparator #(.width(32)) comparator_12 (.a(EX_PC), .b(Tag3), .eq(comparator_12_eq));  // open: gt, lt
  Comparator #(.width(32)) comparator_13 (.a(EX_PC), .b(Tag4), .eq(comparator_13_eq));  // open: gt, lt
  Comparator #(.width(32)) comparator_14 (.a(EX_PC), .b(Tag5), .eq(comparator_14_eq));  // open: gt, lt
  Comparator #(.width(32)) comparator_15 (.a(EX_PC), .b(Tag6), .eq(comparator_15_eq));  // open: gt, lt
  Comparator #(.width(32)) comparator_16 (.a(EX_PC), .b(Tag7), .eq(comparator_16_eq));  // open: gt, lt
  or or_9 (or_10_out[1], and_17_out, and_18_out);
  or or_10 (or_10_out[0], and_19_out, and_20_out);
  Multiplexer #(.select(2), .width(32), .enable("false")) multiplexer_1 (
    .in0(adder_1_out), .in1(adder_1_out), .in2(BranchAddr), .in3(BranchAddr), .out(multiplexer_1_out),
    .sel(PredictSel));
  and and_21 (Replace0, comparator_9_eq, V0);
  and and_22 (Replace1, comparator_10_eq, V1);
  and and_23 (Replace2, comparator_11_eq, V2);
  and and_24 (Replace3, comparator_12_eq, V3);
  and and_25 (Replace4, comparator_13_eq, V4);
  and and_26 (Replace5, comparator_14_eq, V5);
  and and_27 (Replace6, comparator_15_eq, V6);
  and and_28 (Replace7, comparator_16_eq, V7);
  Multiplexer #(.width(2), .enable("false")) multiplexer_2 (
    .in0(or_10_out), .in1(2'b10), .out(NextState), .sel(Replace));
  Multiplexer #(.width(32), .disabled(0), .enable("false")) multiplexer_3 (
    .in0(multiplexer_1_out), .in1(adder_1_out), .out(PredictAddr), .sel(Miss));
  not not_6 (Miss, Hit);
  ExactlyOne xor_1 (.out(Hit), .in0(L0), .in1(L1), .in2(L2), .in3(L3), .in4(L4), .in5(L5), .in6(L6), .in7(L7));
  ExactlyOne xor_2 (
    .out(Refresh), .in0(Replace0), .in1(Replace1), .in2(Replace2), .in3(Replace3), .in4(Replace4),
    .in5(Replace5), .in6(Replace6), .in7(Replace7));
  Priority_Encoder priority_encoder_1 (
    .in0(V0), .in1(V1), .in2(V2), .in3(V3), .in4(V4), .in5(V5), .in6(V6), .in7(V7),
    .out(priority_encoder_1_out), .en_in(1'b1), .en_out(priority_encoder_1_en_out));  // open: gs
  and and_29 (and_29_out, V0, V1, V2, V3, V4, V5, V6, V7);
  not not_7 (Replace, Refresh);
  Adder #(.width(3)) adder_2 (.a(priority_encoder_1_out), .b(3'b001), .out(adder_2_out));  // open: cin, cout
  Multiplexer #(.width(3), .enable("false")) multiplexer_4 (
    .in0(adder_2_out), .in1(3'b000), .out(EmptyPos), .sel(priority_encoder_1_en_out));
  Max3 max3_1 (.Y(C1), .X(C0), .Y_num(3'b001), .X_num(3'b000), .MAX(max3_1_max), .Max_num(max3_1_max_num));
  Max3 max3_2 (
    .Y(max3_3_max), .X(max3_1_max), .Y_num(max3_3_max_num), .X_num(max3_1_max_num), .MAX(max3_2_max),
    .Max_num(max3_2_max_num));
  Max3 max3_3 (.Y(C3), .X(C2), .Y_num(3'b011), .X_num(3'b010), .MAX(max3_3_max), .Max_num(max3_3_max_num));
  Max3 max3_4 (.Y(C5), .X(C4), .Y_num(3'b101), .X_num(3'b100), .MAX(max3_4_max), .Max_num(max3_4_max_num));
  Max3 max3_5 (
    .Y(max3_6_max), .X(max3_4_max), .Y_num(max3_6_max_num), .X_num(max3_4_max_num), .MAX(max3_5_max),
    .Max_num(max3_5_max_num));
  Max3 max3_6 (.Y(C7), .X(C6), .Y_num(3'b111), .X_num(3'b110), .MAX(max3_6_max), .Max_num(max3_6_max_num));
  Max3 max3_7 (
    .Y(max3_5_max), .X(max3_2_max), .Y_num(max3_5_max_num), .X_num(max3_2_max_num), .Max_num(LongestNo));  // open: MAX
  Decoder #(.select(3), .disabled(0)) decoder_1 (
    .out0(Reset0), .out1(Reset1), .out2(Reset2), .out3(Reset3), .out4(Reset4), .out5(Reset5), .out6(Reset6),
    .out7(Reset7), .sel(multiplexer_5_out), .en(and_30_out));
  and and_30 (and_30_out, hasBranch, Replace);
  Multiplexer #(.width(3), .enable("false")) multiplexer_5 (
    .in0(EmptyPos), .in1(LongestNo), .out(multiplexer_5_out), .sel(and_29_out));
  assign {S7, S6, S5, S4, S3, S2, S1, S0} = {Reset7, Reset6, Reset5, Reset4, Reset3, Reset2, Reset1, Reset0} | {Replace7, Replace6, Replace5, Replace4, Replace3, Replace2, Replace1, Replace0};  // OR_Gate or_11, 8 bits wide

  // Other names for the same wires on the sheet: Tag[31:0] = EX_PC

  // Notes on the sheet:
  //   输入引脚区
  //   请勿增改引脚，请勿修改子电路封装
  //   电路功能：利用上面给定的隧道构建8行的Cache，cache映射方式自选
  //   请在下方利用上方输入输出引脚的隧道信号构建电路，ctrl+d复制选择部件
  //   输出引脚区
endmodule

module syn_counter (
  input  add1,
  input  clk,
  input  clr,
  output [15:0] Counter_out
);

  wire [15:0] adder_1_out, multiplexer_1_out, multiplexer_2_out;

  Adder #(.width(16)) adder_1 (.a(Counter_out), .b(16'h1), .out(adder_1_out));  // open: cin, cout
  Multiplexer #(.width(16), .enable("false")) multiplexer_1 (
    .in0(Counter_out), .in1(adder_1_out), .out(multiplexer_1_out), .sel(add1));
  Multiplexer #(.width(16), .enable("false")) multiplexer_2 (
    .in0(multiplexer_1_out), .in1({16{1'b0}}), .out(multiplexer_2_out), .sel(clr));
  Register #(.width(16)) register_1 (.D(multiplexer_2_out), .Q(Counter_out), .clk(clk));  // open: en, clr
endmodule

module test (
  input  Success,
  input  State1,
  input  State0,
  output NextState1,
  output NextState0
);

  wire and_1_out, and_2_out, and_3_out, and_4_out, not_1_out, not_2_out, not_3_out, not_4_out, not_5_out;

  not not_1 (not_1_out, State0);
  not not_2 (not_2_out, Success);
  not not_3 (not_3_out, State0);
  not not_4 (not_4_out, State1);
  not not_5 (not_5_out, State0);
  and and_1 (and_1_out, State1, not_1_out);
  and and_2 (and_2_out, Success, State0);
  and and_3 (and_3_out, not_2_out, State1, not_3_out);
  and and_4 (and_4_out, Success, not_4_out, not_5_out);
  or or_1 (NextState1, and_1_out, and_2_out);
  or or_2 (NextState0, and_3_out, and_4_out);
endmodule
