// Logisim project Cal People.circ as structural Verilog: 8 circuits, main circuit 四位二进制可逆计数器
module \四位二进制可逆计数器  (
  input  CPd,
  input  CPu,
  input  CLR,
  output Sd,
  output Sc,
  output Sb,
  output Sa
);

  wire and_1_out, and_2_out, and_3_out, and_4_out, d_ff_1_qn, d_ff_2_qn, d_ff_3_qn, d_ff_4_qn, not_1_out,
       not_2_out, xor_1_out, xor_2_out, xor_3_out;

  not not_1 (not_1_out, CPd);
  not not_2 (not_2_out, CPu);
  xor xor_1 (xor_1_out, not_2_out, d_ff_2_qn);
  xor xor_2 (xor_2_out, not_2_out, d_ff_3_qn);
  xor xor_3 (xor_3_out, not_2_out, d_ff_4_qn);
  and and_1 (and_1_out, not_1_out, not_2_out);
  and and_2 (and_2_out, xor_1_out, not_2_out);
  and and_3 (and_3_out, xor_2_out, not_2_out);
  and and_4 (and_4_out, xor_3_out, not_2_out);
  D_Flip_Flop d_ff_1 (.clk(and_2_out), .D(d_ff_1_qn), .Q(Sd), .Qn(d_ff_1_qn), .preset(1'b0), .en(1'b1), .reset(CLR));
  D_Flip_Flop d_ff_2 (.clk(and_3_out), .D(d_ff_2_qn), .Q(Sc), .Qn(d_ff_2_qn), .preset(1'b0), .en(1'b1), .reset(CLR));
  D_Flip_Flop d_ff_3 (.clk(and_4_out), .D(d_ff_3_qn), .Q(Sb), .Qn(d_ff_3_qn), .preset(1'b0), .en(1'b1), .reset(CLR));
  D_Flip_Flop d_ff_4 (.clk(and_1_out), .D(d_ff_4_qn), .Q(Sa), .Qn(d_ff_4_qn), .preset(1'b0), .en(1'b1), .reset(CLR));
endmodule

module \四位二进制可逆计数器_测试电路  (
  input  in_1,
  input  in_2,
  input  in_3,
  output out_4,
  output out_5,
  output out_6,
  output out_7
);

  \四位二进制可逆计数器  \u_四位二进制可逆计数器_1  (.Sd(out_4), .Sc(out_5), .Sb(out_6), .Sa(out_7), .CPd(in_3), .CPu(in_1), .CLR(in_2));
endmodule

module \二进制转BCD_15以内  (
  input  Sd,
  input  Sc,
  input  Sb,
  input  Sa,
  output H4,
  output H3,
  output H2,
  output H1,
  output L4,
  output L3,
  output L2,
  output L1
);

  wire and_1_out, or_1_out;

  or or_1 (or_1_out, Sb, Sc);
  and and_1 (and_1_out, Sd, or_1_out);
  \先行进位四位二进制并行加法器  \u_先行进位四位二进制并行加法器_1  (
    .A3(1'b0), .B3(Sd), .A2(and_1_out), .B2(Sc), .A1(and_1_out), .B1(Sb), .A0(1'b0), .B0(Sa), .Ci(1'b0),
    .C4(H1), .S3(L4), .S2(L3), .S1(L2), .S0(L1));

  assign H2 = 1'b0;
  assign H3 = 1'b0;
  assign H4 = 1'b0;
endmodule

module \_7段译码器  (
  input  D,
  input  C,
  input  B,
  input  A,
  output g,
  output f,
  output e,
  output d_2,
  output c_2,
  output b_2,
  output a_2
);

  wire nand_1_out, nand_2_out, nand_3_out, nand_4_out, nand_5_out, nand_6_out, nand_7_out, not_1_out,
       not_2_out, not_3_out, not_4_out, xor_1_out, xor_2_out, xor_3_out, xor_4_out;

  not not_1 (not_1_out, D);
  not not_2 (not_2_out, A);
  not not_3 (not_3_out, B);
  not not_4 (not_4_out, C);
  nand nand_1 (nand_1_out, B, A);
  nand nand_2 (nand_2_out, A, C);
  nand nand_3 (nand_3_out, not_2_out, B);
  xor xor_1 (xor_1_out, not_3_out, C);
  nand nand_4 (nand_4_out, C, nand_1_out);
  nand nand_5 (nand_5_out, not_3_out, not_2_out);
  nand nand_6 (nand_6_out, not_3_out, C);
  nand nand_7 (nand_7_out, not_2_out, not_3_out, not_4_out);
  xor xor_2 (xor_2_out, B, nand_2_out);
  xor xor_3 (xor_3_out, A, B);
  xor xor_4 (xor_4_out, C, A);
  nand nand_8 (g, not_1_out, nand_3_out, xor_1_out);
  nand nand_9 (f, not_1_out, nand_4_out, nand_5_out);
  and and_1 (e, not_2_out, nand_6_out);
  nand nand_10 (d_2, not_1_out, nand_7_out, xor_2_out);
  nand nand_11 (c_2, not_2_out, not_4_out, B);
  nand nand_12 (b_2, C, xor_3_out);
  nand nand_13 (a_2, xor_4_out, not_1_out, not_3_out);
endmodule

module \_7段译码器显示人数  (
  input  in_1,
  input  in_2,
  input  in_3,
  input  in_4
);

  wire \n7段译码器_1_a_2 , \n7段译码器_1_b_2 , \n7段译码器_1_c_2 , \n7段译码器_1_d_2 , \n7段译码器_1_e , \n7段译码器_1_f ,
       \n7段译码器_1_g , \n7段译码器_2_a_2 , \n7段译码器_2_b_2 , \n7段译码器_2_c_2 , \n7段译码器_2_d_2 , \n7段译码器_2_e ,
       \n7段译码器_2_f , \n7段译码器_2_g , \二进制转bcd_15以内_1_h1 , \二进制转bcd_15以内_1_h2 , \二进制转bcd_15以内_1_h3 ,
       \二进制转bcd_15以内_1_h4 , \二进制转bcd_15以内_1_l1 , \二进制转bcd_15以内_1_l2 , \二进制转bcd_15以内_1_l3 ,
       \二进制转bcd_15以内_1_l4 ;

  \二进制转BCD_15以内  \u_二进制转bcd_15以内_1  (
    .Sd(in_1), .Sc(in_2), .Sb(in_3), .Sa(in_4), .H4(\二进制转bcd_15以内_1_h4 ), .H3(\二进制转bcd_15以内_1_h3 ),
    .H2(\二进制转bcd_15以内_1_h2 ), .H1(\二进制转bcd_15以内_1_h1 ), .L4(\二进制转bcd_15以内_1_l4 ), .L3(\二进制转bcd_15以内_1_l3 ),
    .L2(\二进制转bcd_15以内_1_l2 ), .L1(\二进制转bcd_15以内_1_l1 ));
  \_7段译码器  \u_7段译码器_1  (
    .g(\n7段译码器_1_g ), .f(\n7段译码器_1_f ), .e(\n7段译码器_1_e ), .d_2(\n7段译码器_1_d_2 ), .c_2(\n7段译码器_1_c_2 ),
    .b_2(\n7段译码器_1_b_2 ), .a_2(\n7段译码器_1_a_2 ), .D(\二进制转bcd_15以内_1_h4 ), .C(\二进制转bcd_15以内_1_h3 ),
    .B(\二进制转bcd_15以内_1_h2 ), .A(\二进制转bcd_15以内_1_h1 ));
  \_7段译码器  \u_7段译码器_2  (
    .g(\n7段译码器_2_g ), .f(\n7段译码器_2_f ), .e(\n7段译码器_2_e ), .d_2(\n7段译码器_2_d_2 ), .c_2(\n7段译码器_2_c_2 ),
    .b_2(\n7段译码器_2_b_2 ), .a_2(\n7段译码器_2_a_2 ), .D(\二进制转bcd_15以内_1_l4 ), .C(\二进制转bcd_15以内_1_l3 ),
    .B(\二进制转bcd_15以内_1_l2 ), .A(\二进制转bcd_15以内_1_l1 ));
  _7_Segment_Display u_7_segment_display_1 (
    .g(\n7段译码器_1_g ), .f(\n7段译码器_1_f ), .a(\n7段译码器_1_a_2 ), .b(\n7段译码器_1_b_2 ), .e(\n7段译码器_1_e ),
    .d(\n7段译码器_1_d_2 ), .c(\n7段译码器_1_c_2 ));  // open: dp
  _7_Segment_Display u_7_segment_display_2 (
    .g(\n7段译码器_2_g ), .f(\n7段译码器_2_f ), .a(\n7段译码器_2_a_2 ), .b(\n7段译码器_2_b_2 ), .e(\n7段译码器_2_e ),
    .d(\n7段译码器_2_d_2 ), .c(\n7段译码器_2_c_2 ));  // open: dp
endmodule

module \报警电路  (
  input  In,
  input  Cl,
  input  De,
  output W
);

  wire and_1_out, and_2_out, nand_1_out, not_1_out, or_1_out, \四位二进制可逆计数器_1_sa , \四位二进制可逆计数器_1_sb ,
       \四位二进制可逆计数器_1_sc , \四位二进制可逆计数器_1_sd ;

  and and_1 (and_1_out, nand_1_out, In);
  nand nand_1 (nand_1_out, \四位二进制可逆计数器_1_sd , \四位二进制可逆计数器_1_sc , \四位二进制可逆计数器_1_sb , \四位二进制可逆计数器_1_sa );
  and and_2 (and_2_out, or_1_out, De);
  or or_1 (or_1_out, \四位二进制可逆计数器_1_sd , \四位二进制可逆计数器_1_sc , \四位二进制可逆计数器_1_sb , \四位二进制可逆计数器_1_sa );
  \四位二进制可逆计数器  \u_四位二进制可逆计数器_1  (
    .Sd(\四位二进制可逆计数器_1_sd ), .Sc(\四位二进制可逆计数器_1_sc ), .Sb(\四位二进制可逆计数器_1_sb ), .Sa(\四位二进制可逆计数器_1_sa ),
    .CPd(and_2_out), .CPu(and_1_out), .CLR(Cl));
  not not_1 (not_1_out, nand_1_out);
  and and_3 (W, not_1_out, In);
endmodule

module \门禁系统  (
  input  in_1,
  input  in_2,
  input  in_3,
  output out_4,
  output out_5,
  output out_6,
  output out_7,
  output out_8,
  output out_9,
  output out_10,
  output out_11,
  output out_12,
  output out_13,
  output out_14,
  output out_15,
  output out_16,
  output out_17,
  output out_18
);

  wire and_1_out, and_2_out, nand_1_out, not_1_out, or_1_out, \二进制转bcd_15以内_1_h1 , \二进制转bcd_15以内_1_h2 ,
       \二进制转bcd_15以内_1_h3 , \二进制转bcd_15以内_1_h4 , \二进制转bcd_15以内_1_l1 , \二进制转bcd_15以内_1_l2 ,
       \二进制转bcd_15以内_1_l3 , \二进制转bcd_15以内_1_l4 , \四位二进制可逆计数器_1_sa , \四位二进制可逆计数器_1_sb , \四位二进制可逆计数器_1_sc ,
       \四位二进制可逆计数器_1_sd ;

  and and_1 (and_1_out, nand_1_out, in_1);
  nand nand_1 (nand_1_out, \四位二进制可逆计数器_1_sd , \四位二进制可逆计数器_1_sc , \四位二进制可逆计数器_1_sb , \四位二进制可逆计数器_1_sa );
  and and_2 (and_2_out, or_1_out, in_3);
  or or_1 (or_1_out, \四位二进制可逆计数器_1_sd , \四位二进制可逆计数器_1_sc , \四位二进制可逆计数器_1_sb , \四位二进制可逆计数器_1_sa );
  \四位二进制可逆计数器  \u_四位二进制可逆计数器_1  (
    .Sd(\四位二进制可逆计数器_1_sd ), .Sc(\四位二进制可逆计数器_1_sc ), .Sb(\四位二进制可逆计数器_1_sb ), .Sa(\四位二进制可逆计数器_1_sa ),
    .CPd(and_2_out), .CPu(and_1_out), .CLR(in_2));
  not not_1 (not_1_out, nand_1_out);
  and and_3 (out_18, not_1_out, in_1);
  \二进制转BCD_15以内  \u_二进制转bcd_15以内_1  (
    .Sd(\四位二进制可逆计数器_1_sd ), .Sc(\四位二进制可逆计数器_1_sc ), .Sb(\四位二进制可逆计数器_1_sb ), .Sa(\四位二进制可逆计数器_1_sa ),
    .H4(\二进制转bcd_15以内_1_h4 ), .H3(\二进制转bcd_15以内_1_h3 ), .H2(\二进制转bcd_15以内_1_h2 ), .H1(\二进制转bcd_15以内_1_h1 ),
    .L4(\二进制转bcd_15以内_1_l4 ), .L3(\二进制转bcd_15以内_1_l3 ), .L2(\二进制转bcd_15以内_1_l2 ), .L1(\二进制转bcd_15以内_1_l1 ));
  \_7段译码器  \u_7段译码器_1  (
    .g(out_4), .f(out_5), .e(out_6), .d_2(out_7), .c_2(out_8), .b_2(out_9), .a_2(out_10),
    .D(\二进制转bcd_15以内_1_h4 ), .C(\二进制转bcd_15以内_1_h3 ), .B(\二进制转bcd_15以内_1_h2 ), .A(\二进制转bcd_15以内_1_h1 ));
  \_7段译码器  \u_7段译码器_2  (
    .g(out_11), .f(out_12), .e(out_13), .d_2(out_14), .c_2(out_15), .b_2(out_16), .a_2(out_17),
    .D(\二进制转bcd_15以内_1_l4 ), .C(\二进制转bcd_15以内_1_l3 ), .B(\二进制转bcd_15以内_1_l2 ), .A(\二进制转bcd_15以内_1_l1 ));
endmodule

module \门禁系统测试电路  (
  input  in_1,
  input  in_2,
  input  in_3
);

  wire \门禁系统_1_out_4 , \门禁系统_1_out_5 , \门禁系统_1_out_6 , \门禁系统_1_out_7 , \门禁系统_1_out_8 , \门禁系统_1_out_9 ,
       \门禁系统_1_out_10 , \门禁系统_1_out_11 , \门禁系统_1_out_12 , \门禁系统_1_out_13 , \门禁系统_1_out_14 , \门禁系统_1_out_15 ,
       \门禁系统_1_out_16 , \门禁系统_1_out_17 , \门禁系统_1_out_18 ;

  _7_Segment_Display u_7_segment_display_1 (
    .g(\门禁系统_1_out_4 ), .f(\门禁系统_1_out_5 ), .a(\门禁系统_1_out_10 ), .b(\门禁系统_1_out_9 ), .e(\门禁系统_1_out_6 ),
    .d(\门禁系统_1_out_7 ), .c(\门禁系统_1_out_8 ));  // open: dp
  \门禁系统  \u_门禁系统_1  (
    .out_4(\门禁系统_1_out_4 ), .out_5(\门禁系统_1_out_5 ), .out_6(\门禁系统_1_out_6 ), .out_7(\门禁系统_1_out_7 ),
    .out_8(\门禁系统_1_out_8 ), .out_9(\门禁系统_1_out_9 ), .out_10(\门禁系统_1_out_10 ), .out_11(\门禁系统_1_out_11 ),
    .out_12(\门禁系统_1_out_12 ), .out_13(\门禁系统_1_out_13 ), .out_14(\门禁系统_1_out_14 ), .out_15(\门禁系统_1_out_15 ),
    .out_16(\门禁系统_1_out_16 ), .out_17(\门禁系统_1_out_17 ), .in_1(in_1), .in_2(in_2), .in_3(in_3),
    .out_18(\门禁系统_1_out_18 ));
  _7_Segment_Display u_7_segment_display_2 (
    .g(\门禁系统_1_out_11 ), .f(\门禁系统_1_out_12 ), .a(\门禁系统_1_out_17 ), .b(\门禁系统_1_out_16 ), .e(\门禁系统_1_out_13 ),
    .d(\门禁系统_1_out_14 ), .c(\门禁系统_1_out_15 ));  // open: dp
  LED led_1 (.in(\门禁系统_1_out_18 ));
endmodule
