// Logisim project 数电大作业.circ as structural Verilog: 5 circuits, main circuit main
module main (
  input  in_1,
  input  in_2,
  input  in_3
);

  wire A_out_6, A_out_7, A_out_8, A_out_9, and_1_out, and_2_out, and_3_out, and_4_out, and_5_out, and_6_out,
       and_7_out, and_8_out, and_9_out, and_10_out, B_out_6, B_out_7, B_out_8, B_out_9, C_out_6, C_out_7,
       C_out_8, C_out_9, D_out_6, D_out_7, D_out_8, D_out_9, not_1_out, not_2_out, not_3_out, select_1_out_4,
       select_2_out_4, select_3_out_4, select_4_out_4, select_5_out_4, select_6_out_4, select_7_out_4,
       select_8_out_4, xor_1_out, xor_2_out, xor_3_out, xor_4_out, xor_5_out, xor_6_out, xor_7_out,
       xor_8_out, \先行进位四位二进制并行加法器_1_s0 , \先行进位四位二进制并行加法器_1_s1 , \先行进位四位二进制并行加法器_1_s2 , \先行进位四位二进制并行加法器_1_s3 ;

  and and_1 (and_1_out, in_1, not_1_out);
  and and_2 (and_2_out, in_1, in_2);
  not not_1 (not_1_out, in_2);
  not not_2 (not_2_out, in_3);
  and and_3 (and_3_out, and_1_out, not_2_out);
  LED led_1 (.in(select_1_out_4));
  select select_1 (.in_1(in_2), .out_4(select_1_out_4), .in_2(select_4_out_4), .in_3(\先行进位四位二进制并行加法器_1_s3 ));
  \先行进位四位二进制并行加法器  \u_先行进位四位二进制并行加法器_1  (
    .A3(A_out_6), .B3(xor_1_out), .A2(A_out_7), .B2(xor_2_out), .A1(A_out_8), .B1(xor_4_out), .A0(A_out_9),
    .B0(xor_3_out), .Ci(in_3), .S3(\先行进位四位二进制并行加法器_1_s3 ), .S2(\先行进位四位二进制并行加法器_1_s2 ),
    .S1(\先行进位四位二进制并行加法器_1_s1 ), .S0(\先行进位四位二进制并行加法器_1_s0 ));  // open: C4
  rigister A (
    .in_1(and_3_out), .in_2(\先行进位四位二进制并行加法器_1_s3 ), .in_3(\先行进位四位二进制并行加法器_1_s2 ),
    .in_4(\先行进位四位二进制并行加法器_1_s1 ), .in_5(\先行进位四位二进制并行加法器_1_s0 ), .out_6(A_out_6), .out_7(A_out_7),
    .out_8(A_out_8), .out_9(A_out_9));
  LED led_2 (.in(select_2_out_4));
  select select_2 (.in_1(in_2), .out_4(select_2_out_4), .in_2(select_5_out_4), .in_3(\先行进位四位二进制并行加法器_1_s2 ));
  xor xor_1 (xor_1_out, B_out_6, in_3);
  xor xor_2 (xor_2_out, B_out_7, in_3);
  and and_4 (and_4_out, in_3, and_1_out);
  rigister B (
    .in_1(and_4_out), .in_2(\先行进位四位二进制并行加法器_1_s3 ), .in_3(\先行进位四位二进制并行加法器_1_s2 ),
    .in_4(\先行进位四位二进制并行加法器_1_s1 ), .in_5(\先行进位四位二进制并行加法器_1_s0 ), .out_6(B_out_6), .out_7(B_out_7),
    .out_8(B_out_8), .out_9(B_out_9));
  xor xor_3 (xor_3_out, B_out_9, in_3);
  xor xor_4 (xor_4_out, B_out_8, in_3);
  and and_5 (and_5_out, and_2_out, not_3_out);
  not not_3 (not_3_out, in_3);
  LED led_3 (.in(select_3_out_4));
  select select_3 (.in_1(in_2), .out_4(select_3_out_4), .in_2(select_6_out_4), .in_3(\先行进位四位二进制并行加法器_1_s1 ));
  select select_4 (.in_1(in_3), .out_4(select_4_out_4), .in_2(xor_5_out), .in_3(and_8_out));
  select select_5 (.in_1(in_3), .out_4(select_5_out_4), .in_2(xor_8_out), .in_3(and_6_out));
  and and_6 (and_6_out, A_out_7, C_out_7);
  and and_7 (and_7_out, C_out_8, A_out_8);
  and and_8 (and_8_out, A_out_6, C_out_6);
  rigister C (
    .in_1(and_5_out), .in_2(select_4_out_4), .in_3(select_5_out_4), .in_4(select_6_out_4),
    .in_5(select_8_out_4), .out_6(C_out_6), .out_7(C_out_7), .out_8(C_out_8), .out_9(C_out_9));
  select select_6 (.in_1(in_3), .out_4(select_6_out_4), .in_2(xor_7_out), .in_3(and_7_out));
  xor xor_5 (xor_5_out, A_out_6, D_out_6);
  and and_9 (and_9_out, C_out_9, A_out_9);
  and and_10 (and_10_out, in_3, and_2_out);
  LED led_4 (.in(select_7_out_4));
  select select_7 (.in_1(in_2), .out_4(select_7_out_4), .in_2(select_8_out_4), .in_3(\先行进位四位二进制并行加法器_1_s0 ));
  select select_8 (.in_1(in_3), .out_4(select_8_out_4), .in_2(xor_6_out), .in_3(and_9_out));
  xor xor_6 (xor_6_out, D_out_9, A_out_9);
  xor xor_7 (xor_7_out, D_out_8, A_out_8);
  xor xor_8 (xor_8_out, A_out_7, D_out_7);
  rigister D (
    .in_1(and_10_out), .in_2(select_4_out_4), .in_3(select_5_out_4), .in_4(select_6_out_4),
    .in_5(select_8_out_4), .out_6(D_out_6), .out_7(D_out_7), .out_8(D_out_8), .out_9(D_out_9));
endmodule

module rigister (
  input  in_1,
  input  in_2,
  input  in_3,
  input  in_4,
  input  in_5,
  output out_6,
  output out_7,
  output out_8,
  output out_9
);

  D_Flip_Flop d_ff_1 (.clk(in_1), .D(in_2), .Q(out_6));  // open: Qn, preset, en, reset
  D_Flip_Flop d_ff_2 (.clk(in_1), .D(in_3), .Q(out_7));  // open: Qn, preset, en, reset
  D_Flip_Flop d_ff_3 (.clk(in_1), .D(in_4), .Q(out_8));  // open: Qn, preset, en, reset
  D_Flip_Flop d_ff_4 (.clk(in_1), .D(in_5), .Q(out_9));  // open: Qn, preset, en, reset
endmodule

module select (
  input  in_1,
  input  in_2,
  input  in_3,
  output out_4
);

  wire and_1_out, and_2_out, not_1_out;

  or or_1 (out_4, and_1_out, and_2_out);
  and and_1 (and_1_out, in_1, in_2);
  and and_2 (and_2_out, not_1_out, in_3);
  not not_1 (not_1_out, in_1);
endmodule

module \new  (
  input  in_1,
  input  in_2,
  input  in_3
);

  wire A_out_6, A_out_7, A_out_8, A_out_9, and_1_out, and_2_out, and_3_out, and_4_out, and_5_out, and_6_out,
       and_7_out, and_8_out, and_9_out, and_10_out, B_out_6, B_out_7, B_out_8, B_out_9, C_out_6, C_out_7,
       C_out_8, C_out_9, D_out_6, D_out_7, D_out_8, D_out_9, not_1_out, not_2_out, not_3_out,
       select4_1_out_10, select4_1_out_11, select4_1_out_12, select4_1_out_13, select4_2_out_10,
       select4_2_out_11, select4_2_out_13, xor_1_out, xor_2_out, xor_3_out, xor_4_out, xor_5_out, xor_6_out,
       xor_7_out, xor_8_out, \先行进位四位二进制并行加法器_1_s0 , \先行进位四位二进制并行加法器_1_s1 , \先行进位四位二进制并行加法器_1_s2 ,
       \先行进位四位二进制并行加法器_1_s3 ;

  and and_1 (and_1_out, in_1, not_1_out);
  and and_2 (and_2_out, in_1, in_2);
  not not_1 (not_1_out, in_2);
  not not_2 (not_2_out, in_3);
  and and_3 (and_3_out, and_1_out, not_2_out);
  \先行进位四位二进制并行加法器  \u_先行进位四位二进制并行加法器_1  (
    .A3(A_out_6), .B3(xor_1_out), .A2(A_out_7), .B2(xor_2_out), .A1(A_out_8), .B1(xor_4_out), .A0(A_out_9),
    .B0(xor_3_out), .Ci(in_3), .S3(\先行进位四位二进制并行加法器_1_s3 ), .S2(\先行进位四位二进制并行加法器_1_s2 ),
    .S1(\先行进位四位二进制并行加法器_1_s1 ), .S0(\先行进位四位二进制并行加法器_1_s0 ));  // open: C4
  rigister A (
    .in_1(and_3_out), .in_2(\先行进位四位二进制并行加法器_1_s3 ), .in_3(\先行进位四位二进制并行加法器_1_s2 ),
    .in_4(\先行进位四位二进制并行加法器_1_s1 ), .in_5(\先行进位四位二进制并行加法器_1_s0 ), .out_6(A_out_6), .out_7(A_out_7),
    .out_8(A_out_8), .out_9(A_out_9));
  xor xor_1 (xor_1_out, B_out_6, in_3);
  xor xor_2 (xor_2_out, B_out_7, in_3);
  and and_4 (and_4_out, in_3, and_1_out);
  rigister B (
    .in_1(and_4_out), .in_2(\先行进位四位二进制并行加法器_1_s3 ), .in_3(\先行进位四位二进制并行加法器_1_s2 ),
    .in_4(\先行进位四位二进制并行加法器_1_s1 ), .in_5(\先行进位四位二进制并行加法器_1_s0 ), .out_6(B_out_6), .out_7(B_out_7),
    .out_8(B_out_8), .out_9(B_out_9));
  LED led_1 (.in(select4_1_out_10));
  select4 select4_1 (
    .out_10(select4_1_out_10), .out_11(select4_1_out_11), .out_12(select4_1_out_12),
    .out_13(select4_1_out_13), .in_1(in_2), .in_2(\先行进位四位二进制并行加法器_1_s3 ), .in_3(\先行进位四位二进制并行加法器_1_s2 ),
    .in_4(\先行进位四位二进制并行加法器_1_s1 ), .in_5(\先行进位四位二进制并行加法器_1_s0 ), .in_6(select4_2_out_10),
    .in_7(select4_2_out_11), .in_8(select4_2_out_11), .in_9(select4_2_out_13));
  xor xor_3 (xor_3_out, B_out_9, in_3);
  xor xor_4 (xor_4_out, B_out_8, in_3);
  LED led_2 (.in(select4_1_out_11));
  LED led_3 (.in(select4_1_out_13));
  LED led_4 (.in(select4_1_out_12));
  and and_5 (and_5_out, and_2_out, not_3_out);
  not not_3 (not_3_out, in_3);
  and and_6 (and_6_out, A_out_6, C_out_6);
  and and_7 (and_7_out, C_out_8, A_out_8);
  and and_8 (and_8_out, A_out_7, C_out_7);
  rigister C (
    .in_1(and_5_out), .in_2(select4_2_out_10), .in_3(select4_2_out_11), .in_4(select4_2_out_11),
    .in_5(select4_2_out_13), .out_6(C_out_6), .out_7(C_out_7), .out_8(C_out_8), .out_9(C_out_9));
  select4 select4_2 (
    .out_10(select4_2_out_10), .out_11(select4_2_out_11), .out_12(select4_2_out_11),
    .out_13(select4_2_out_13), .in_1(in_3), .in_2(and_6_out), .in_3(and_8_out), .in_4(and_7_out),
    .in_5(and_9_out), .in_6(xor_5_out), .in_7(xor_7_out), .in_8(xor_8_out), .in_9(xor_6_out));
  xor xor_5 (xor_5_out, A_out_6, D_out_6);
  and and_9 (and_9_out, C_out_9, A_out_9);
  and and_10 (and_10_out, in_3, and_2_out);
  xor xor_6 (xor_6_out, D_out_9, A_out_9);
  xor xor_7 (xor_7_out, A_out_7, D_out_7);
  xor xor_8 (xor_8_out, D_out_8, A_out_8);
  rigister D (
    .in_1(and_10_out), .in_2(select4_2_out_10), .in_3(select4_2_out_11), .in_4(select4_2_out_11),
    .in_5(select4_2_out_13), .out_6(D_out_6), .out_7(D_out_7), .out_8(D_out_8), .out_9(D_out_9));
endmodule

module select4 (
  input  in_1,
  input  in_2,
  input  in_3,
  input  in_4,
  input  in_5,
  input  in_6,
  input  in_7,
  input  in_8,
  input  in_9,
  output out_10,
  output out_11,
  output out_12,
  output out_13
);

  wire and_1_out, and_2_out, and_3_out, and_4_out, and_5_out, and_6_out, and_7_out, and_8_out, not_1_out;

  and and_1 (and_1_out, not_1_out, in_2);
  not not_1 (not_1_out, in_1);
  or or_1 (out_10, and_1_out, and_2_out);
  and and_2 (and_2_out, in_1, in_3);
  or or_2 (out_11, and_3_out, and_4_out);
  and and_3 (and_3_out, not_1_out, in_4);
  and and_4 (and_4_out, in_1, in_5);
  or or_3 (out_12, and_5_out, and_6_out);
  and and_5 (and_5_out, not_1_out, in_6);
  and and_6 (and_6_out, in_1, in_7);
  and and_7 (and_7_out, not_1_out, in_8);
  or or_4 (out_13, and_7_out, and_8_out);
  and and_8 (and_8_out, in_1, in_9);
endmodule
