// Logisim project 系列二进制加法器.circ as structural Verilog: 6 circuits, main circuit 半加器
module \半加器  (
  input  A,
  input  B,
  output C,
  output S
);

  and and_1 (C, A, B);
  xor xor_1 (S, A, B);
endmodule

module \全加器_利用半加器实现  (
  input  A,
  input  B,
  input  Ci,
  output Co,
  output S
);

  wire \半加器_1_c , \半加器_1_s , \半加器_2_c ;

  \半加器  \u_半加器_1  (.A(A), .B(B), .C(\半加器_1_c ), .S(\半加器_1_s ));
  \半加器  \u_半加器_2  (.A(\半加器_1_s ), .B(Ci), .C(\半加器_2_c ), .S(S));
  or or_1 (Co, \半加器_1_c , \半加器_2_c );
endmodule

module \全加器_利用基本逻辑门实现  (
  input  A,
  input  B,
  input  Ci,
  output S,
  output Co
);

  wire nand_1_out, nand_2_out, nand_3_out, xor_1_out;

  xor xor_1 (xor_1_out, A, B);
  nand nand_1 (nand_1_out, A, B);
  nand nand_2 (nand_2_out, A, Ci);
  nand nand_3 (nand_3_out, B, Ci);
  nand nand_4 (Co, nand_1_out, nand_2_out, nand_3_out);
  xor xor_2 (S, xor_1_out, Ci);
endmodule

module \串行进位四位二进制并行加法器  (
  input  A3,
  input  B3,
  input  A2,
  input  B2,
  input  A1,
  input  B1,
  input  A0,
  input  B0,
  input  Ci,
  output C4,
  output S3,
  output S2,
  output S1,
  output S0
);

  wire \全加器_利用基本逻辑门实现_1_co , \全加器_利用基本逻辑门实现_2_co , \全加器_利用基本逻辑门实现_3_co ;

  \全加器_利用基本逻辑门实现  \u_全加器_利用基本逻辑门实现_1  (.A(A0), .B(B0), .Ci(Ci), .S(S0), .Co(\全加器_利用基本逻辑门实现_1_co ));
  \全加器_利用基本逻辑门实现  \u_全加器_利用基本逻辑门实现_2  (.A(A1), .B(B1), .Ci(\全加器_利用基本逻辑门实现_1_co ), .S(S1), .Co(\全加器_利用基本逻辑门实现_2_co ));
  \全加器_利用基本逻辑门实现  \u_全加器_利用基本逻辑门实现_3  (.A(A2), .B(B2), .Ci(\全加器_利用基本逻辑门实现_2_co ), .S(S2), .Co(\全加器_利用基本逻辑门实现_3_co ));
  \全加器_利用基本逻辑门实现  \u_全加器_利用基本逻辑门实现_4  (.A(A3), .B(B3), .Ci(\全加器_利用基本逻辑门实现_3_co ), .S(S3), .Co(C4));
endmodule

module \先行进位四位二进制并行加法器  (
  input  A3,
  input  B3,
  input  A2,
  input  B2,
  input  A1,
  input  B1,
  input  A0,
  input  B0,
  input  Ci,
  output C4,
  output S3,
  output S2,
  output S1,
  output S0
);

  wire and_1_out, and_2_out, and_3_out, and_4_out, and_5_out, and_6_out, and_7_out, and_8_out, and_9_out,
       and_10_out, G1_out, G2_out, G3_out, G4_out, or_2_out, or_3_out, or_4_out, P1_out, P2_out, P3_out,
       P4_out;

  and G4 (G4_out, A3, B3);
  and G3 (G3_out, A2, B2);
  and G2 (G2_out, A1, B1);
  and G1 (G1_out, A0, B0);
  xor P4 (P4_out, A3, B3);
  xor P3 (P3_out, A2, B2);
  xor P2 (P2_out, A1, B1);
  xor P1 (P1_out, A0, B0);
  and and_1 (and_1_out, P4_out, G3_out);
  and and_2 (and_2_out, P4_out, P3_out, G2_out);
  and and_3 (and_3_out, P4_out, P3_out, P2_out, G1_out);
  and and_4 (and_4_out, P4_out, P3_out, P2_out, P1_out, Ci);
  and and_5 (and_5_out, P3_out, G2_out);
  and and_6 (and_6_out, P3_out, P2_out, G1_out);
  and and_7 (and_7_out, P3_out, P2_out, P1_out, Ci);
  and and_8 (and_8_out, P2_out, G1_out);
  and and_9 (and_9_out, P2_out, P1_out, Ci);
  and and_10 (and_10_out, P1_out, Ci);
  or or_1 (C4, G4_out, and_1_out, and_2_out, and_3_out, and_4_out);
  or or_2 (or_2_out, G3_out, and_5_out, and_6_out, and_7_out);
  or or_3 (or_3_out, G2_out, and_8_out, and_9_out);
  or or_4 (or_4_out, G1_out, and_10_out);
  xor xor_1 (S3, P4_out, or_2_out);
  xor xor_2 (S2, P3_out, or_3_out);
  xor xor_3 (S1, P2_out, or_4_out);
  xor xor_4 (S0, P1_out, Ci);
endmodule

module \先行进位四位二进制并行加法器_测试电路  (
  input  in_1,
  input  in_2,
  input  in_3,
  input  in_4,
  input  in_5,
  input  in_6,
  input  in_7,
  input  in_8,
  input  in_9,
  output out_10,
  output out_11,
  output out_12,
  output out_13,
  output out_14
);

  \先行进位四位二进制并行加法器  \u_先行进位四位二进制并行加法器_1  (
    .A3(in_1), .B3(in_5), .A2(in_2), .B2(in_6), .A1(in_3), .B1(in_7), .A0(in_4), .B0(in_8), .Ci(in_9),
    .C4(out_10), .S3(out_11), .S2(out_12), .S1(out_13), .S0(out_14));
endmodule
